// Logisim project ALU.circ as structural Verilog
module ALU (
  input  [31:0] A,
  input  [3:0] Op_Selector,
  input  [31:0] B,
  output Division_By_Zero_Flag,
  output Zero_flag,
  output Negative_flag,
  output Carry_flag,
  output [31:0] out_8
);

  wire A___B_s, A___B_uns, adder_1_cout, subtractor_1_bout;
  wire [31:0] adder_1_out, and_1_out, divider_1_out, HI_Signed, HI_Unsigned, multiplexer_1_out,
       multiplexer_2_out, multiplier_1_out, NOR_out, OR_out, signed_division_1_out_4,
       signed_multiplier_1_out_4, subtractor_1_out, XOR_out;

  Adder #(.width(32)) adder_1 (.a(A), .b(B), .out(adder_1_out), .cin(1'b0), .cout(adder_1_cout));
  Subtractor #(.width(32)) subtractor_1 (.a(A), .b(B), .out(subtractor_1_out), .bin(1'b0), .bout(subtractor_1_bout));
  Signed_multiplier signed_multiplier_1 (
    .in_1(A), .in_3(B), .out_4(signed_multiplier_1_out_4), .out_5(HI_Signed), .in_2({32{1'b0}}));
  Multiplier #(.width(32)) multiplier_1 (.a(A), .b(B), .out(multiplier_1_out), .cin({32{1'b0}}), .cout(HI_Unsigned));
  Divider #(.width(32)) divider_1 (.a(A), .b(B), .out(divider_1_out), .upper({32{1'b0}}));  // open: rem
  Signed_division signed_division_1 (
    .in_1(A), .in_3(B), .out_4(signed_division_1_out_4), .in_2({32{1'b0}}));  // open: out_5
  assign and_1_out = A & B;  // AND_Gate and_1, 32 bits wide
  assign OR_out = A | B;  // OR_Gate OR, 32 bits wide
  assign NOR_out = ~(A | B);  // NOR_Gate NOR, 32 bits wide
  assign XOR_out = A ^ B;  // XOR_Gate XOR, 32 bits wide
  Multiplexer #(.width(32), .enable("false")) multiplexer_1 (
    .in0({32{1'b0}}), .in1(32'h1), .out(multiplexer_1_out), .sel(A___B_uns));
  Multiplexer #(.width(32), .enable("false")) multiplexer_2 (
    .in0({32{1'b0}}), .in1(32'h1), .out(multiplexer_2_out), .sel(A___B_s));
  Multiplexer #(.enable("false")) multiplexer_3 (
    .in0(adder_1_cout), .in1(subtractor_1_bout), .out(Carry_flag), .sel(Op_Selector[0]));
  Is_zero_32_bits is_zero_32_bits_1 (.in_1(out_8), .out_2(Zero_flag));
  Multiplexer #(.select(4), .width(32), .enable("false")) multiplexer_4 (
    .in0(adder_1_out), .in1(subtractor_1_out), .in2(signed_multiplier_1_out_4), .in3(multiplier_1_out),
    .in4(divider_1_out), .in5(signed_division_1_out_4), .in6(and_1_out), .in7(OR_out), .in8(NOR_out),
    .in9(XOR_out), .in10(multiplexer_1_out), .in11(multiplexer_2_out), .in12(HI_Signed), .in13(HI_Unsigned),
    .in14({32{1'b0}}), .in15({32{1'b0}}), .out(out_8), .sel(Op_Selector));
  Is_negative_32_bits is_negative_32_bits_1 (.in_1(out_8), .out_2(Negative_flag));
  Comparator #(.width(32), .mode("unsigned")) comparator_1 (.a(A), .b(B), .lt(A___B_uns));  // open: gt, eq
  Is_zero_32_bits is_zero_32_bits_2 (.in_1(B), .out_2(Division_By_Zero_Flag));
  Comparator #(.width(32)) comparator_2 (.a(A), .b(B), .lt(A___B_s));  // open: gt, eq

  // Other names for the same wires on the sheet: Carry_Out = Carry_flag; Is_Negative = Negative_flag;
  //   Is_Zero = Zero_flag; Sum_Selector = Op_Selector[0]

  // Notes on the sheet:
  //   Entradas vacías son conectadas a 0
  //   is B zero
  //   Unsigned comparator
  //   Signed comparator
endmodule

// MOD
module Module (
  input  [31:0] in_1,
  output [31:0] out_2
);

  wire [31:0] comp_2_1_out_2;

  // Probe on in_1
  Comp_2 comp_2_1 (.in_1(in_1), .out_2(comp_2_1_out_2));  // open: out_3
  Multiplexer #(.width(32), .enable("false")) multiplexer_1 (
    .in0(in_1), .in1(comp_2_1_out_2), .out(out_2), .sel(in_1[31]));
  // Probe on out_2

  // Other names for the same wires on the sheet: b_sign = in_1[31]
endmodule

// Comp
module Comp_2 (
  input  [31:0] in_1,
  output [31:0] out_2,
  output out_3
);

  wire [31:0] not_1_out;

  // Probe on in_1
  assign not_1_out = ~in_1;  // NOT_Gate not_1, 32 bits wide
  Adder #(.width(32)) adder_1 (.a(not_1_out), .b({32{1'b0}}), .out(out_2), .cin(1'b1), .cout(out_3));
  // Probe on out_2
endmodule

// Sign X
module Signed_multiplier (
  input  [31:0] in_1,
  input  [31:0] in_2,
  input  [31:0] in_3,
  output [31:0] out_4,
  output [31:0] out_5
);

  wire comp_2_1_out_3, res_sign;
  wire [31:0] adder_1_out, comp_2_1_out_2, module_1_out_2, module_2_out_2, multiplier_1_cout,
       multiplier_1_out, not_1_out;

  // Probe on in_1
  // Probe on in_3
  Module module_1 (.in_1(in_1), .out_2(module_1_out_2));
  Module module_2 (.in_1(in_3), .out_2(module_2_out_2));
  Multiplier #(.width(32)) multiplier_1 (
    .a(module_1_out_2), .b(module_2_out_2), .out(multiplier_1_out), .cin(in_2), .cout(multiplier_1_cout));
  xor xor_1 (res_sign, in_1[31], in_3[31]);
  Comp_2 comp_2_1 (.in_1(multiplier_1_out), .out_2(comp_2_1_out_2), .out_3(comp_2_1_out_3));
  assign not_1_out = ~multiplier_1_cout;  // NOT_Gate not_1, 32 bits wide
  // Probe on res_sign
  Adder #(.width(32)) adder_1 (.a(not_1_out), .b({32{1'b0}}), .out(adder_1_out), .cin(comp_2_1_out_3));  // open: cout
  // Probe on out_4
  Multiplexer #(.width(32), .enable("false")) multiplexer_1 (
    .in0(multiplier_1_out), .in1(comp_2_1_out_2), .out(out_4), .sel(res_sign));
  Multiplexer #(.width(32), .enable("false")) multiplexer_2 (
    .in0(multiplier_1_cout), .in1(adder_1_out), .out(out_5), .sel(res_sign));
  // Probe on out_5

  // Other names for the same wires on the sheet: a_sign = in_1[31]; b_sign = in_3[31]
endmodule

module Signed_division (
  input  [31:0] in_1,
  input  [31:0] in_2,
  input  [31:0] in_3,
  output [31:0] out_4,
  output [31:0] out_5
);

  wire res_sign;
  wire [31:0] comp_2_1_out_2, comp_2_2_out_2, divider_1_out, divider_1_rem, module_1_out_2, module_2_out_2;

  // Probe on in_1
  // Probe on in_3
  Module module_1 (.in_1(in_1), .out_2(module_1_out_2));
  Module module_2 (.in_1(in_3), .out_2(module_2_out_2));
  Divider #(.width(32)) divider_1 (
    .a(module_1_out_2), .b(module_2_out_2), .out(divider_1_out), .upper(in_2), .rem(divider_1_rem));
  xor xor_1 (res_sign, in_1[31], in_3[31]);
  // Probe on res_sign
  Comp_2 comp_2_1 (.in_1(divider_1_out), .out_2(comp_2_1_out_2));  // open: out_3
  // Probe on out_4
  Multiplexer #(.width(32), .enable("false")) multiplexer_1 (
    .in0(divider_1_out), .in1(comp_2_1_out_2), .out(out_4), .sel(res_sign));
  Multiplexer #(.width(32), .enable("false")) multiplexer_2 (
    .in0(divider_1_rem), .in1(comp_2_2_out_2), .out(out_5), .sel(in_1[31]));
  Comp_2 comp_2_2 (.in_1(divider_1_rem), .out_2(comp_2_2_out_2));  // open: out_3
  // Probe on out_5

  // Other names for the same wires on the sheet: a_sign = in_1[31]; b_sign = in_3[31]
endmodule

module is_zero_2_bits (
  input  [1:0] in_1,
  output out_2
);

  wire [1:0] not_1_out;

  assign not_1_out = ~in_1;  // NOT_Gate not_1, 2 bits wide
  and and_1 (out_2, not_1_out[0], not_1_out[1]);
endmodule

module is_zero_4_bits (
  input  [3:0] in_1,
  output out_2
);

  wire is_zero_2_bits_1_out_2, is_zero_2_bits_2_out_2;

  is_zero_2_bits is_zero_2_bits_1 (.in_1(in_1[1:0]), .out_2(is_zero_2_bits_1_out_2));
  and and_1 (out_2, is_zero_2_bits_1_out_2, is_zero_2_bits_2_out_2);
  is_zero_2_bits is_zero_2_bits_2 (.in_1(in_1[3:2]), .out_2(is_zero_2_bits_2_out_2));
endmodule

module is_zero_8_bits (
  input  [7:0] in_1,
  output out_2
);

  wire is_zero_4_bits_1_out_2, is_zero_4_bits_2_out_2;

  is_zero_4_bits is_zero_4_bits_1 (.in_1(in_1[3:0]), .out_2(is_zero_4_bits_1_out_2));
  is_zero_4_bits is_zero_4_bits_2 (.in_1(in_1[7:4]), .out_2(is_zero_4_bits_2_out_2));
  and and_1 (out_2, is_zero_4_bits_1_out_2, is_zero_4_bits_2_out_2);
endmodule

module is_zero_16_bits (
  input  [15:0] in_1,
  output out_2
);

  wire is_zero_8_bits_1_out_2, is_zero_8_bits_2_out_2;

  is_zero_8_bits is_zero_8_bits_1 (.in_1(in_1[7:0]), .out_2(is_zero_8_bits_1_out_2));
  is_zero_8_bits is_zero_8_bits_2 (.in_1(in_1[15:8]), .out_2(is_zero_8_bits_2_out_2));
  and and_1 (out_2, is_zero_8_bits_1_out_2, is_zero_8_bits_2_out_2);
endmodule

module Is_zero_32_bits (
  input  [31:0] in_1,
  output out_2
);

  wire is_zero_16_bits_1_out_2, is_zero_16_bits_2_out_2;

  is_zero_16_bits is_zero_16_bits_1 (.in_1(in_1[15:0]), .out_2(is_zero_16_bits_1_out_2));
  is_zero_16_bits is_zero_16_bits_2 (.in_1(in_1[31:16]), .out_2(is_zero_16_bits_2_out_2));
  and and_1 (out_2, is_zero_16_bits_1_out_2, is_zero_16_bits_2_out_2);
endmodule

module Is_negative_32_bits (
  input  [31:0] in_1,
  output out_2
);


  assign out_2 = in_1[31];
endmodule
