// Logisim project ALU(Finished).circ as structural Verilog
module old_alu_eliminar (
  input  [31:0] A,
  input  [31:0] B,
  input  [3:0] in_3,
  output Division_By_Zero_Flag,
  output Zero_flag,
  output Negative_flag,
  output Carry_flag,
  output [31:0] out_8,
  output NOP,
  output UPDATE_HI_LO,
  output [31:0] HI_CONTENT,
  output [31:0] LO_CONTENT
);

  wire A___B_s, A___B_uns, adder_1_cout, not_1_out, subtractor_1_bout;
  wire [31:0] adder_1_out, and_1_out, HI___Signed, HI___Unsigned, HI_X_Signed, HI_X_Unsigned, LO___Signed,
       LO___Unsigned, LO_X_Signed, LO_X_Unsigned, multiplexer_1_out, multiplexer_2_out, multiplexer_6_out,
       NOR_out, OR_out, subtractor_1_out, XOR_out;

  Adder #(.width(32)) adder_1 (.a(A), .b(B), .out(adder_1_out), .cin(1'b0), .cout(adder_1_cout));
  Subtractor #(.width(32)) subtractor_1 (.a(A), .b(B), .out(subtractor_1_out), .bin(1'b0), .bout(subtractor_1_bout));
  assign and_1_out = A & B;  // AND_Gate and_1, 32 bits wide
  assign OR_out = A | B;  // OR_Gate OR, 32 bits wide
  assign NOR_out = ~(A | B);  // NOR_Gate NOR, 32 bits wide
  assign XOR_out = A ^ B;  // XOR_Gate XOR, 32 bits wide
  Multiplexer #(.width(32), .enable("false")) multiplexer_1 (
    .in0({32{1'b0}}), .in1(32'h1), .out(multiplexer_1_out), .sel(A___B_uns));
  Multiplexer #(.width(32), .enable("false")) multiplexer_2 (
    .in0({32{1'b0}}), .in1(32'h1), .out(multiplexer_2_out), .sel(A___B_s));
  Signed_multiplier signed_multiplier_1 (
    .in_1(A), .in_3(B), .out_4(LO_X_Signed), .out_5(HI_X_Signed), .in_2({32{1'b0}}));
  Multiplier #(.width(32)) multiplier_1 (.a(A), .b(B), .out(LO_X_Unsigned), .cin({32{1'b0}}), .cout(HI_X_Unsigned));
  // Signed_division signed_division_1: pin names not known; wires that end beside it: A, B, {32{1'b0}}, HI___Signed, LO___Signed
  Divider #(.width(32)) divider_1 (.a(A), .b(B), .out(LO___Unsigned), .upper({32{1'b0}}), .rem(HI___Unsigned));
  Multiplexer #(.enable("false")) multiplexer_3 (
    .in0(adder_1_cout), .in1(subtractor_1_bout), .out(Carry_flag), .sel(in_3[0]));
  is_zero_4_bits is_zero_4_bits_1 (.in_1(in_3), .out_2(NOP));
  Multiplexer #(.select(2), .width(32), .enable("false")) multiplexer_4 (
    .in0(HI_X_Signed), .in1(HI_X_Unsigned), .in2(HI___Signed), .in3(HI___Unsigned), .out(HI_CONTENT),
    .sel(in_3[1:0]));
  Multiplexer #(.select(2), .width(32), .enable("false")) multiplexer_5 (
    .in0(LO_X_Signed), .in1(LO_X_Unsigned), .in2(LO___Signed), .in3(LO___Unsigned), .out(LO_CONTENT),
    .sel(in_3[1:0]));
  Multiplexer #(.select(3), .width(32), .enable("false")) multiplexer_6 (
    .in0(adder_1_out), .in1(subtractor_1_out), .in2(and_1_out), .in3(OR_out), .in4(NOR_out), .in5(XOR_out),
    .in6(multiplexer_1_out), .in7(multiplexer_2_out), .out(multiplexer_6_out), .sel(in_3[2:0]));
  Is_zero_32_bits is_zero_32_bits_1 (.in_1(out_8), .out_2(Zero_flag));
  Multiplexer #(.width(32), .enable("false")) multiplexer_7 (
    .in0({32{1'b0}}), .in1(multiplexer_6_out), .out(out_8), .sel(in_3[3]));
  Comparator #(.width(32), .mode("unsigned")) comparator_1 (.a(A), .b(B), .lt(A___B_uns));  // open: gt, eq
  Is_zero_32_bits is_zero_32_bits_2 (.in_1(B), .out_2(Division_By_Zero_Flag));
  Is_negative_32_bits__eliminar is_negative_32_bits_eliminar_1 (.in_1(out_8), .out_2(Negative_flag));
  not not_1 (not_1_out, in_3[3]);
  and and_2 (UPDATE_HI_LO, in_3[2], not_1_out);
  Comparator #(.width(32)) comparator_2 (.a(A), .b(B), .lt(A___B_s));  // open: gt, eq

  // Other names for the same wires on the sheet: Carry_Out = Carry_flag; hi_ops[1:0] = in_3[1:0];
  //   op_bits[2:0] = in_3[2:0]; Sum_Selector = in_3[0]; Is_Negative = Negative_flag; Is_Zero = Zero_flag

  // Notes on the sheet:
  //   HI MULTIPLEXOR
  //   LO MULTIPLEXOR
  //   Falta Mayor, menor o igual, y igual igual, y debo sacarlo por el grande
  //   is B zero
  //   Unsigned comparator
  //   Signed comparator
endmodule

// MOD
module Module (
  input  [31:0] in_1,
  output [31:0] out_2
);

  wire [31:0] comp_2_1_out_2;

  // Probe on in_1
  Comp_2 comp_2_1 (.in_1(in_1), .out_2(comp_2_1_out_2));  // open: out_3
  Multiplexer #(.width(32), .enable("false")) multiplexer_1 (
    .in0(in_1), .in1(comp_2_1_out_2), .out(out_2), .sel(in_1[31]));
  // Probe on out_2

  // Other names for the same wires on the sheet: b_sign = in_1[31]
endmodule

// Comp
module Comp_2 (
  input  [31:0] in_1,
  output [31:0] out_2,
  output out_3
);

  wire [31:0] not_1_out;

  // Probe on in_1
  assign not_1_out = ~in_1;  // NOT_Gate not_1, 32 bits wide
  Adder #(.width(32)) adder_1 (.a(not_1_out), .b({32{1'b0}}), .out(out_2), .cin(1'b1), .cout(out_3));
  // Probe on out_2
endmodule

// Sign X
module Signed_multiplier (
  input  [31:0] in_1,
  input  [31:0] in_2,
  input  [31:0] in_3,
  output [31:0] out_4,
  output [31:0] out_5
);

  wire comp_2_1_out_3, res_sign;
  wire [31:0] adder_1_out, comp_2_1_out_2, module_1_out_2, module_2_out_2, multiplier_1_cout,
       multiplier_1_out, not_1_out;

  // Probe on in_1
  // Probe on in_3
  Module module_1 (.in_1(in_1), .out_2(module_1_out_2));
  Module module_2 (.in_1(in_3), .out_2(module_2_out_2));
  Multiplier #(.width(32)) multiplier_1 (
    .a(module_1_out_2), .b(module_2_out_2), .out(multiplier_1_out), .cin(in_2), .cout(multiplier_1_cout));
  xor xor_1 (res_sign, in_1[31], in_3[31]);
  Comp_2 comp_2_1 (.in_1(multiplier_1_out), .out_2(comp_2_1_out_2), .out_3(comp_2_1_out_3));
  assign not_1_out = ~multiplier_1_cout;  // NOT_Gate not_1, 32 bits wide
  // Probe on res_sign
  Adder #(.width(32)) adder_1 (.a(not_1_out), .b({32{1'b0}}), .out(adder_1_out), .cin(comp_2_1_out_3));  // open: cout
  // Probe on out_4
  Multiplexer #(.width(32), .enable("false")) multiplexer_1 (
    .in0(multiplier_1_out), .in1(comp_2_1_out_2), .out(out_4), .sel(res_sign));
  Multiplexer #(.width(32), .enable("false")) multiplexer_2 (
    .in0(multiplier_1_cout), .in1(adder_1_out), .out(out_5), .sel(res_sign));
  // Probe on out_5

  // Other names for the same wires on the sheet: a_sign = in_1[31]; b_sign = in_3[31]
endmodule

module Signed_division (
  input  [31:0] A,
  input  [31:0] superior,
  input  [31:0] B,
  output [31:0] \output ,
  output [31:0] resto
);

  wire res_sign;
  wire [31:0] comp_2_1_out_2, comp_2_2_out_2, divider_1_out, divider_1_rem, module_1_out_2, module_2_out_2;

  // Probe on A
  // Probe on B
  Module module_1 (.in_1(A), .out_2(module_1_out_2));
  Module module_2 (.in_1(B), .out_2(module_2_out_2));
  Divider #(.width(32)) divider_1 (
    .a(module_1_out_2), .b(module_2_out_2), .out(divider_1_out), .upper(superior), .rem(divider_1_rem));
  xor xor_1 (res_sign, A[31], B[31]);
  // Probe on res_sign
  Comp_2 comp_2_1 (.in_1(divider_1_out), .out_2(comp_2_1_out_2));  // open: out_3
  // Probe on \output 
  Multiplexer #(.width(32), .enable("false")) multiplexer_1 (
    .in0(divider_1_out), .in1(comp_2_1_out_2), .out(\output ), .sel(res_sign));
  Multiplexer #(.width(32), .enable("false")) multiplexer_2 (
    .in0(divider_1_rem), .in1(comp_2_2_out_2), .out(resto), .sel(A[31]));
  Comp_2 comp_2_2 (.in_1(divider_1_rem), .out_2(comp_2_2_out_2));  // open: out_3
  // Probe on resto

  // Other names for the same wires on the sheet: a_sign = A[31]; b_sign = B[31]
endmodule

module is_zero_2_bits (
  input  [1:0] in_1,
  output out_2
);

  wire [1:0] not_1_out;

  assign not_1_out = ~in_1;  // NOT_Gate not_1, 2 bits wide
  and and_1 (out_2, not_1_out[0], not_1_out[1]);
endmodule

module is_zero_4_bits (
  input  [3:0] in_1,
  output out_2
);

  wire is_zero_2_bits_1_out_2, is_zero_2_bits_2_out_2;

  is_zero_2_bits is_zero_2_bits_1 (.in_1(in_1[1:0]), .out_2(is_zero_2_bits_1_out_2));
  and and_1 (out_2, is_zero_2_bits_1_out_2, is_zero_2_bits_2_out_2);
  is_zero_2_bits is_zero_2_bits_2 (.in_1(in_1[3:2]), .out_2(is_zero_2_bits_2_out_2));
endmodule

module is_zero_8_bits (
  input  [7:0] in_1,
  output out_2
);

  wire is_zero_4_bits_1_out_2, is_zero_4_bits_2_out_2;

  is_zero_4_bits is_zero_4_bits_1 (.in_1(in_1[3:0]), .out_2(is_zero_4_bits_1_out_2));
  is_zero_4_bits is_zero_4_bits_2 (.in_1(in_1[7:4]), .out_2(is_zero_4_bits_2_out_2));
  and and_1 (out_2, is_zero_4_bits_1_out_2, is_zero_4_bits_2_out_2);
endmodule

module is_zero_16_bits (
  input  [15:0] in_1,
  output out_2
);

  wire is_zero_8_bits_1_out_2, is_zero_8_bits_2_out_2;

  is_zero_8_bits is_zero_8_bits_1 (.in_1(in_1[7:0]), .out_2(is_zero_8_bits_1_out_2));
  is_zero_8_bits is_zero_8_bits_2 (.in_1(in_1[15:8]), .out_2(is_zero_8_bits_2_out_2));
  and and_1 (out_2, is_zero_8_bits_1_out_2, is_zero_8_bits_2_out_2);
endmodule

module Is_zero_32_bits (
  input  [31:0] in_1,
  output out_2
);

  wire is_zero_16_bits_1_out_2, is_zero_16_bits_2_out_2;

  is_zero_16_bits is_zero_16_bits_1 (.in_1(in_1[15:0]), .out_2(is_zero_16_bits_1_out_2));
  is_zero_16_bits is_zero_16_bits_2 (.in_1(in_1[31:16]), .out_2(is_zero_16_bits_2_out_2));
  and and_1 (out_2, is_zero_16_bits_1_out_2, is_zero_16_bits_2_out_2);
endmodule

module Is_negative_32_bits__eliminar (
  input  [31:0] in_1,
  output out_2
);


  assign out_2 = in_1[31];
endmodule

module ALU (
  input  [31:0] A,
  input  [31:0] B,
  input  [3:0] Op,
  output [31:0] HI_CONTENT,
  output UPDATE_HI_LO,
  output [31:0] Output,
  output [31:0] LO_CONTENT,
  output B_ZERO
);

  wire A____B, A___B_s, A___B_s_t, not_1_out, Sub_Cout, Sum_Cout;
  wire [31:0] And, Equal, Gt, HI___Signed, HI___Unsigned, HI_X_Signed, HI_X_Unsigned, LO___Signed,
       LO___Unsigned, LO_X_Signed, LO_X_Unsigned, Lt_signed, Lt_uns, Lte, Nor, Or, Sub, Sum, Xor;

  Adder #(.width(32)) adder_1 (.a(A), .b(B), .out(Sum), .cin(1'b0), .cout(Sum_Cout));
  Subtractor #(.width(32)) subtractor_1 (.a(A), .b(B), .out(Sub), .bin(1'b0), .bout(Sub_Cout));
  Signed_multiplier signed_multiplier_1 (
    .in_1(A), .in_3(B), .out_4(LO_X_Signed), .out_5(HI_X_Signed), .in_2({32{1'b0}}));
  Multiplier #(.width(32)) multiplier_1 (.a(A), .b(B), .out(LO_X_Unsigned), .cin({32{1'b0}}), .cout(HI_X_Unsigned));
  Divider #(.width(32)) divider_1 (.a(A), .b(B), .out(LO___Unsigned), .upper({32{1'b0}}), .rem(HI___Unsigned));
  assign And = A & B;  // AND_Gate and_1, 32 bits wide
  assign Or = A | B;  // OR_Gate OR, 32 bits wide
  Signed_division signed_division_1 (.A(A), .B(B), .\output (LO___Signed), .resto(HI___Signed), .superior({32{1'b0}}));
  assign Nor = ~(A | B);  // NOR_Gate NOR, 32 bits wide
  assign Xor = A ^ B;  // XOR_Gate XOR, 32 bits wide
  Multiplexer #(.select(2), .width(32), .enable("false")) multiplexer_1 (
    .in0(HI_X_Signed), .in1(HI_X_Unsigned), .in2(HI___Signed), .in3(HI___Unsigned), .out(HI_CONTENT),
    .sel(Op[1:0]));
  Multiplexer #(.select(2), .width(32), .enable("false")) multiplexer_2 (
    .in0(LO_X_Signed), .in1(LO_X_Unsigned), .in2(LO___Signed), .in3(LO___Unsigned), .out(LO_CONTENT),
    .sel(Op[1:0]));
  Multiplexer #(.width(32), .enable("false")) multiplexer_3 (
    .in0({32{1'b0}}), .in1(32'h1), .out(Lt_uns), .sel(Sub_Cout));
  Multiplexer #(.width(32), .enable("false")) multiplexer_4 (
    .in0({32{1'b0}}), .in1(32'h1), .out(Lt_signed), .sel(A___B_s));
  and and_2 (UPDATE_HI_LO, Op[2], ~Op[3]);  // AND_Gate
  Is_zero_32_bits is_zero_32_bits_1 (.in_1(B), .out_2(B_ZERO));
  Multiplexer #(.width(32), .enable("false")) multiplexer_5 (.in0({32{1'b0}}), .in1(32'h1), .out(Equal), .sel(A____B));
  Comparator #(.width(32)) comparator_1 (.a(A), .b(B), .gt(A___B_s_t), .eq(A____B), .lt(A___B_s));
  Multiplexer #(.width(32), .enable("false")) multiplexer_6 (.in0({32{1'b0}}), .in1(32'h1), .out(Gt), .sel(A___B_s_t));
  Multiplexer #(.select(4), .width(32), .enable("false")) multiplexer_7 (
    .in0({32{1'b0}}), .in1(Gt), .in2(Lte), .in3(Equal), .in4({32{1'b0}}), .in5({32{1'b0}}), .in6({32{1'b0}}),
    .in7({32{1'b0}}), .in8(Sum), .in9(Sub), .in10(And), .in11(Or), .in12(Nor), .in13(Xor), .in14(Lt_uns),
    .in15(Lt_signed), .out(Output), .sel(Op));
  not not_1 (not_1_out, A___B_s_t);
  Multiplexer #(.width(32), .enable("false")) multiplexer_8 (.in0({32{1'b0}}), .in1(32'h1), .out(Lte), .sel(not_1_out));

  // Other names for the same wires on the sheet: hi_ops[1:0] = Op[1:0]

  // Notes on the sheet:
  //   INPUTS
  //   ALU
  //   Signed
  //   Unsigned
  //   Multiply
  //   Addition and substraction
  //   Division
  //   Logic Operations
  //   HI MULTIPLEXOR
  //   LO MULTIPLEXOR
  //   Comparations
  //   A < B unsigned
  //   A < B signed
  //   FLAGS
  //   A == B 
  //   Signed comparator
  //   A > B 
  //   ALU OUTPUT
  //   A <= B 
endmodule
