// Logisim project BranchControl(FInished).circ as structural Verilog
module RegisterFile (
  input  [4:0] DA_DestinationAddress,
  input  [31:0] DI_DataInput,
  input  RW_Read_Write,
  input  Rst_Reset,
  input  [4:0] SA,
  input  [4:0] SB,
  output [31:0] Out_A,
  output [31:0] Out_B
);

  wire and_1_out, and_2_out, and_3_out, and_4_out, and_5_out, and_6_out, and_7_out, and_8_out, and_9_out,
       and_10_out, and_11_out, and_12_out, and_13_out, and_14_out, and_15_out, and_16_out, and_17_out,
       and_18_out, and_19_out, and_20_out, and_21_out, and_22_out, and_23_out, and_24_out, and_25_out,
       and_26_out, and_27_out, and_28_out, and_29_out, and_30_out, and_31_out, and_32_out, clk, E_R00, E_R01,
       E_R02, E_R03, E_R04, E_R05, E_R06, E_R07, E_R08, E_R09, E_R10, E_R11, E_R12, E_R13, E_R14, E_R15,
       E_R16, E_R17, E_R18, E_R19, E_R20, E_R21, E_R22, E_R23, E_R24, E_R25, E_R26, E_R27, E_R28, E_R29,
       E_R30, E_R31;
  wire [31:0] O_R00, O_R01, O_R02, O_R03, O_R04, O_R05, O_R06, O_R07, O_R08, O_R09, O_R10, O_R11, O_R12,
       O_R13, O_R14, O_R15, O_R16, O_R17, O_R18, O_R19, O_R20, O_R21, O_R22, O_R23, O_R24, O_R25, O_R26,
       O_R27, O_R28, O_R29, O_R30, O_R31;

  Clock clock_1 (.out(clk));
  Decoder #(.select(5), .enable("false")) decoder_1 (
    .out0(E_R00), .out1(E_R01), .out2(E_R02), .out3(E_R03), .out4(E_R04), .out5(E_R05), .out6(E_R06),
    .out7(E_R07), .out8(E_R08), .out9(E_R09), .out10(E_R10), .out11(E_R11), .out12(E_R12), .out13(E_R13),
    .out14(E_R14), .out15(E_R15), .out16(E_R16), .out17(E_R17), .out18(E_R18), .out19(E_R19), .out20(E_R20),
    .out21(E_R21), .out22(E_R22), .out23(E_R23), .out24(E_R24), .out25(E_R25), .out26(E_R26), .out27(E_R27),
    .out28(E_R28), .out29(E_R29), .out30(E_R30), .out31(E_R31), .sel(DA_DestinationAddress));
  and and_1 (and_1_out, E_R00, RW_Read_Write);
  and and_2 (and_2_out, E_R08, RW_Read_Write);
  and and_3 (and_3_out, E_R16, RW_Read_Write);
  and and_4 (and_4_out, E_R24, RW_Read_Write);
  Register #(.width(32)) R0 (.D(DI_DataInput), .en(and_1_out), .Q(O_R00), .clk(clk), .clr(Rst_Reset));
  Register #(.width(32)) R8 (.D(DI_DataInput), .en(and_2_out), .Q(O_R08), .clk(clk), .clr(Rst_Reset));
  Register #(.width(32)) R16 (.D(DI_DataInput), .en(and_3_out), .Q(O_R16), .clk(clk), .clr(Rst_Reset));
  Register #(.width(32)) R24 (.D(DI_DataInput), .en(and_4_out), .Q(O_R24), .clk(clk), .clr(Rst_Reset));
  and and_5 (and_5_out, E_R01, RW_Read_Write);
  and and_6 (and_6_out, E_R09, RW_Read_Write);
  and and_7 (and_7_out, E_R17, RW_Read_Write);
  and and_8 (and_8_out, E_R25, RW_Read_Write);
  Register #(.width(32)) R1 (.D(DI_DataInput), .en(and_5_out), .Q(O_R01), .clk(clk));  // open: clr
  Register #(.width(32)) R9 (.D(DI_DataInput), .en(and_6_out), .Q(O_R09), .clk(clk), .clr(Rst_Reset));
  Register #(.width(32)) R17 (.D(DI_DataInput), .en(and_7_out), .Q(O_R17), .clk(clk));  // open: clr
  Register #(.width(32)) R25 (.D(DI_DataInput), .en(and_8_out), .Q(O_R25), .clk(clk), .clr(Rst_Reset));
  and and_9 (and_9_out, E_R02, RW_Read_Write);
  and and_10 (and_10_out, E_R10, RW_Read_Write);
  and and_11 (and_11_out, E_R18, RW_Read_Write);
  and and_12 (and_12_out, E_R26, RW_Read_Write);
  Register #(.width(32)) R2 (.D(DI_DataInput), .en(and_9_out), .Q(O_R02), .clk(clk), .clr(Rst_Reset));
  Register #(.width(32)) R10 (.D(DI_DataInput), .en(and_10_out), .Q(O_R10), .clk(clk), .clr(Rst_Reset));
  Register #(.width(32)) R18 (.D(DI_DataInput), .en(and_11_out), .Q(O_R18), .clk(clk), .clr(Rst_Reset));
  Register #(.width(32)) R26 (.D(DI_DataInput), .en(and_12_out), .Q(O_R26), .clk(clk), .clr(Rst_Reset));
  and and_13 (and_13_out, E_R03, RW_Read_Write);
  and and_14 (and_14_out, E_R11, RW_Read_Write);
  and and_15 (and_15_out, E_R27, RW_Read_Write);
  Multiplexer #(.select(5), .width(32), .enable("false")) multiplexer_1 (
    .in0(O_R00), .in1(O_R01), .in2(O_R02), .in3(O_R03), .in4(O_R04), .in5(O_R05), .in6(O_R06), .in7(O_R07),
    .in8(O_R08), .in9(O_R09), .in10(O_R10), .in11(O_R11), .in12(O_R12), .in13(O_R13), .in14(O_R14),
    .in15(O_R15), .in16(O_R16), .in17(O_R17), .in18(O_R18), .in19(O_R19), .in20(O_R20), .in21(O_R21),
    .in22(O_R22), .in23(O_R23), .in24(O_R24), .in25(O_R25), .in26(O_R26), .in27(O_R27), .in28(O_R28),
    .in29(O_R29), .in30(O_R30), .in31(O_R31), .out(Out_A), .sel(SA));
  Multiplexer #(.select(5), .width(32), .enable("false")) multiplexer_2 (
    .in0(O_R00), .in1(O_R01), .in2(O_R02), .in3(O_R03), .in4(O_R04), .in5(O_R05), .in6(O_R06), .in7(O_R07),
    .in8(O_R08), .in9(O_R09), .in10(O_R10), .in11(O_R11), .in12(O_R12), .in13(O_R13), .in14(O_R14),
    .in15(O_R15), .in16(O_R16), .in17(O_R17), .in18(O_R18), .in19(O_R19), .in20(O_R20), .in21(O_R21),
    .in22(O_R22), .in23(O_R23), .in24(O_R24), .in25(O_R25), .in26(O_R26), .in27(O_R27), .in28(O_R28),
    .in29(O_R29), .in30(O_R30), .in31(O_R31), .out(Out_B), .sel(SB));
  Register #(.width(32)) R3 (.D(DI_DataInput), .en(and_13_out), .Q(O_R03), .clk(clk), .clr(Rst_Reset));
  Register #(.width(32)) R11 (.D(DI_DataInput), .en(and_14_out), .Q(O_R11), .clk(clk), .clr(Rst_Reset));
  Register #(.width(32)) R19 (.D(DI_DataInput), .en(and_16_out), .Q(O_R19), .clk(clk), .clr(Rst_Reset));
  and and_16 (and_16_out, E_R19, RW_Read_Write);
  Register #(.width(32)) R27 (.D(DI_DataInput), .en(and_15_out), .Q(O_R27), .clk(clk), .clr(Rst_Reset));
  and and_17 (and_17_out, E_R04, RW_Read_Write);
  and and_18 (and_18_out, E_R12, RW_Read_Write);
  and and_19 (and_19_out, E_R20, RW_Read_Write);
  and and_20 (and_20_out, E_R28, RW_Read_Write);
  Register #(.width(32)) R4 (.D(DI_DataInput), .en(and_17_out), .Q(O_R04), .clk(clk), .clr(Rst_Reset));
  Register #(.width(32)) R12 (.D(DI_DataInput), .en(and_18_out), .Q(O_R12), .clk(clk), .clr(Rst_Reset));
  Register #(.width(32)) R20 (.D(DI_DataInput), .en(and_19_out), .Q(O_R20), .clk(clk), .clr(Rst_Reset));
  Register #(.width(32)) R28 (.D(DI_DataInput), .en(and_20_out), .Q(O_R28), .clk(clk), .clr(Rst_Reset));
  and and_21 (and_21_out, E_R05, RW_Read_Write);
  and and_22 (and_22_out, E_R13, RW_Read_Write);
  and and_23 (and_23_out, E_R29, RW_Read_Write);
  Register #(.width(32)) R5 (.D(DI_DataInput), .en(and_21_out), .Q(O_R05), .clk(clk), .clr(Rst_Reset));
  Register #(.width(32)) R13 (.D(DI_DataInput), .en(and_22_out), .Q(O_R13), .clk(clk), .clr(Rst_Reset));
  Register #(.width(32)) R21 (.D(DI_DataInput), .en(and_24_out), .Q(O_R21), .clk(clk), .clr(Rst_Reset));
  and and_24 (and_24_out, E_R21, RW_Read_Write);
  Register #(.width(32)) R29 (.D(DI_DataInput), .en(and_23_out), .Q(O_R29), .clk(clk), .clr(Rst_Reset));
  and and_25 (and_25_out, E_R06, RW_Read_Write);
  and and_26 (and_26_out, E_R14, RW_Read_Write);
  and and_27 (and_27_out, E_R22, RW_Read_Write);
  and and_28 (and_28_out, E_R30, RW_Read_Write);
  Register #(.width(32)) R6 (.D(DI_DataInput), .en(and_25_out), .Q(O_R06), .clk(clk), .clr(Rst_Reset));
  Register #(.width(32)) R14 (.D(DI_DataInput), .en(and_26_out), .Q(O_R14), .clk(clk), .clr(Rst_Reset));
  Register #(.width(32)) R22 (.D(DI_DataInput), .en(and_27_out), .Q(O_R22), .clk(clk), .clr(Rst_Reset));
  Register #(.width(32)) R30 (.D(DI_DataInput), .en(and_28_out), .Q(O_R30), .clk(clk), .clr(Rst_Reset));
  and and_29 (and_29_out, E_R07, RW_Read_Write);
  and and_30 (and_30_out, E_R15, RW_Read_Write);
  and and_31 (and_31_out, E_R31, RW_Read_Write);
  Register #(.width(32)) R7 (.D(DI_DataInput), .en(and_29_out), .Q(O_R07), .clk(clk), .clr(Rst_Reset));
  Register #(.width(32)) R15 (.D(DI_DataInput), .en(and_30_out), .Q(O_R15), .clk(clk), .clr(Rst_Reset));
  Register #(.width(32)) R23 (.D(DI_DataInput), .en(and_32_out), .Q(O_R23), .clk(clk), .clr(Rst_Reset));
  and and_32 (and_32_out, E_R23, RW_Read_Write);
  Register #(.width(32)) R31 (.D(DI_DataInput), .en(and_31_out), .Q(O_R31), .clk(clk), .clr(Rst_Reset));

  // Other names for the same wires on the sheet: DI[31:0] = DI_DataInput; R = Rst_Reset; R_W = RW_Read_Write
endmodule

module BranchControl (
  input  [1:0] jmp,
  input  FC_FlagCondition,
  input  [1:0] JS_JumpSize,
  input  [31:0] IA_InstructionAddress
);

  Multiplexer #(.select(2), .enable("false")) multiplexer_1 ();  // open: in0, in1, in2, in3, out, sel

  // Notes on the sheet:
  //   jmp Legend
  //   00 -> nop
  //   10 -> j
  //   11 -> jr
  //   01 -> beq, bne, blez, bgtz, bltz
endmodule

module ProgramCounter (
  input  [31:0] jmp_addr,
  input  jmp_Jump,
  input  rst_Reset,
  output [31:0] Q
);

  wire clk_out;
  wire [31:0] adder_1_out, multiplexer_1_out;

  Clock clk (.out(clk_out));
  Register #(.width(32)) register_1 (.D(multiplexer_1_out), .en(1'b1), .Q(Q), .clk(clk_out), .clr(rst_Reset));
  Adder #(.width(32)) adder_1 (.a(Q), .b(32'h4), .out(adder_1_out));  // open: cin, cout
  Multiplexer #(.width(32), .enable("false")) multiplexer_1 (
    .in0(adder_1_out), .in1(jmp_addr), .out(multiplexer_1_out), .sel(jmp_Jump));
endmodule
