// Logisim project Branch_Control(Finished).circ as structural Verilog: 1 circuit, main circuit Branch_Control
module Branch_Control (
  input  [31:0] JS_Jump_Size,
  input  [31:0] IA_InstructionAddress,
  input  jmp,
  input  FC,
  output [31:0] NIR_NextInstructionAddrs
);

  wire and_1_out;
  wire [31:0] adder_1_out, adder_2_out, multiplier_1_out;

  Adder #(.width(32)) adder_1 (.a(IA_InstructionAddress), .b(32'h4), .out(adder_1_out), .cin(1'b0));  // open: cout
  Multiplier #(.width(32)) multiplier_1 (
    .a(JS_Jump_Size), .b(32'h4), .out(multiplier_1_out), .cin({32{1'b0}}));  // open: cout
  Adder #(.width(32)) adder_2 (.a(multiplier_1_out), .b(adder_1_out), .out(adder_2_out), .cin(1'b0));  // open: cout
  and and_1 (and_1_out, jmp, FC);
  Multiplexer #(.width(32), .enable("false")) multiplexer_1 (
    .in0(adder_1_out), .in1(adder_2_out), .out(NIR_NextInstructionAddrs), .sel(and_1_out));

  // Notes on the sheet:
  //   JS x 4
  //   IA + 4
  //   IA + 4 + (JS x 4)
endmodule
