// Logisim project CPU test.circ as structural Verilog: 1 circuit, main circuit CPU
module CPU (
);

  wire Active_E_I, B_Cero, comparator_1_eq, FC, Jmp, Load, R_W, Store, UpdateHi;
  wire [1:0] Esp_Inst;
  wire [3:0] Op;
  wire [4:0] DA, SA, SB;
  wire [15:0] Const;
  wire [25:0] dest;
  wire [31:0] A, ActualInstruction, B, B_prime, DATA_HI, DATA_IN, DATA_LO, JS, jump_address;

  InstructionDecoder instructiondecoder_1 (
    .DA_DataAddress(DA), .R_W_ReadWrite(R_W), .SA_SelectorA(SA), .SB_SelectorB(SB), .Jmp(Jmp),
    .FC_FlagCondition(FC), .dest(dest), .A(Const), .Op(Op), .Load(Load), .Store(Store),
    .Active_EI(Active_E_I), .EspecialInstruction(Esp_Inst));  // open: Instruction, DI_DataInput
  Branch_Control branch_control_1 (.JS(JS), .IA(ActualInstruction), .jmp(Jmp), .FC(FC), .IA_prime(jump_address));
  ProgramCounter programcounter_1 (.jmp_addr(jump_address), .Q(ActualInstruction));  // open: jmp_Jump, rst_Reset
  assign JS = {{16{1'b0}}, Const};  // Bit_Extender bit_extender_1
  Multiplexer #(.width(32), .enable("false")) multiplexer_1 (.in0(B), .in1(JS), .out(B_prime), .sel(comparator_1_eq));
  Comparator #(.width(32), .mode("unsigned")) comparator_1 (
    .a(B), .b({32{1'b0}}), .eq(comparator_1_eq));  // open: gt, lt
  RegisterFile registerfile_1 (
    .DA_DestinationAddress(DA), .DI_DataInput(DATA_IN), .RW_Read_Write(R_W), .SA(SA), .SB(SB), .Out_A(A),
    .Out_B(B));  // open: Rst_Reset
  ALU alu_1 (
    .A(A), .B(B_prime), .Op(Op), .HI_CONTENT(DATA_HI), .UPDATE_HI_LO(UpdateHi), .Output(DATA_IN),
    .LO_CONTENT(DATA_LO), .B_ZERO(B_Cero));
  Hi_Lo_registers_main main_1 (
    .HI_Content(DATA_HI), .Lo_Content(DATA_LO), .Update(UpdateHi));  // open: Reset, Hi_Value, Lo_Value

  // Notes on the sheet:
  //   Agregar al RF las entradas de HI y Lo
  //   Hacer SpecialInstructionManager
endmodule
