// Logisim project CPU(S-MIPS).circ as structural Verilog: 1 circuit, main circuit S-MIPS
module S_MIPS (
  input  [31:0] RAM_Out_0,
  input  [31:0] RAM_Out_1,
  input  [31:0] RAM_Out_2,
  input  [31:0] RAM_Out_3,
  input  [3:0] Read_Time,
  input  [3:0] Write_Time,
  input  Reset,
  input  Clock,
  input  Kbd_Available,
  input  [6:0] Kbd_ASCII_Data,
  output [31:0] RAM_In_0,
  output [31:0] RAM_In_1,
  output [31:0] RAM_In_2,
  output [31:0] RAM_In_3,
  output Halt,
  output [15:0] Address,
  output Kbd_Enable,
  output Kbd_Clear,
  output TTY_Enable,
  output [6:0] TTY_ASCII_Data,
  output [3:0] Mask,
  output nRead_Write,
  output Chip_Select
);

  wire en_MC, Fetch, Fetched, inst_R_W, rnd_kbd, upd;
  wire [2:0] S_FC;
  wire [3:0] ALU_OP, mask_t;
  wire [5:0] FuncCode, OpCode;
  wire [15:0] inst_addrs;
  wire [17:0] SelectorCodes;
  wire [31:0] inp_Word, inst, MemoryAddress, MemoryData, Out_Word;

  // Control_Unit control_unit_1: pin names not known; wires that end beside it: Reset, Fetched, FuncCode, OpCode, Reset, Reset, S_FC, ALU_OP, SelectorCodes, rnd_kbd, TTY_Enable
  InstructionMemory instructionmemory_1 (
    .PC_ProgramCounter(MemoryAddress), .fetch(Fetch), .Word(Out_Word), .upd_InstructionUpdated(upd),
    .rst_reset(Reset), .addrs(inst_addrs), .mask(mask_t), .R_W(inst_R_W), .Chip_Select(en_MC),
    .Instruction(inst), .fetched(Fetched));
  Memory_Controller memory_controller_1 (
    .Address(inst_addrs), .Input_Word(inp_Word), .Mask(mask_t), .O0(RAM_Out_0), .O1(RAM_Out_1),
    .O2(RAM_Out_2), .O3(RAM_Out_3), .R_W(inst_R_W), .Chip_Select(en_MC), .Read_Time(Read_Time),
    .Write_Time(Write_Time), .Address_2(Address), .OW_Out_Word(Out_Word), .Mask_2(Mask), .R_W_2(nRead_Write),
    .CS(Chip_Select), .Updated(upd));  // open: I0, I1, I2, I3
  DataPath datapath_1 (
    .reset(Reset), .KBD_Data(Kbd_ASCII_Data), .KBD_Enable(Kbd_Available), .Memory_Address(MemoryAddress),
    .Instruction(inst), .Selectors_Code(SelectorCodes), .TTY_Data(TTY_ASCII_Data), .MemoryData(Out_Word),
    .Memory_Data_Out(MemoryData), .Op(ALU_OP), .S_FlagCondition(S_FC), .FuncCode(FuncCode), .OpCode(OpCode),
    .rnd_kbd_Selector(rnd_kbd), .fetch(Fetch));  // open: ReadIns, clock

  // Other names for the same wires on the sheet: CLK = Clock; CS = Chip_Select; KBD_AVAIL = Kbd_Available;
  //   KBD_CLR = Kbd_Clear; KBD_DATA[6:0] = Kbd_ASCII_Data; RAM_A[15:0] = Address; RAM_INPUT_0[31:0] = RAM_In_0;
  //   RAM_INPUT_1[31:0] = RAM_In_1; RAM_INPUT_2[31:0] = RAM_In_2; RAM_INPUT_3[31:0] = RAM_In_3; RAM_MASK[3:0] = Mask;
  //   RO0[31:0] = RAM_Out_0; RO1[31:0] = RAM_Out_1; RO2[31:0] = RAM_Out_2; RO3[31:0] = RAM_Out_3; RST = Reset;
  //   RW = nRead_Write; STOP = Halt; TTY_DATA[6:0] = TTY_ASCII_Data

  // Notes on the sheet:
  //   RAM TIMING
  //   KEYBOARD
  //   DATA FROM RAM
  //   RAM ADDRESS
  //   KEYBOARD
  //   TTY
  //   DATA WRITE MASK
  //   RAM CONTROL
  //   DATA TO RAM
endmodule
