// Logisim project Control_Unit.circ as structural Verilog: 1 circuit, main circuit Control Unit
module Control_Unit (
  input  [5:0] FuncCode,
  input  [5:0] OpCode,
  input  START,
  input  Clock,
  input  RamReady,
  output [18:0] SelectorCodes,
  output [2:0] FC_Selector,
  output [3:0] ALU_Op,
  output fetch,
  output rnd_kbd_Selector,
  output TTY_Enable,
  output ReadInstruction,
  output ChipSelect,
  output R_W,
  output halt,
  output kbd_Enable,
  output CRONORST,
  output RESET
);

  wire CS0, CS1, CS2, CS3, CS4, demultiplexer_1_out0, demultiplexer_1_out1, demultiplexer_2_out0,
       demultiplexer_3_out0, demultiplexer_4_out0, demultiplexer_5_out0, demultiplexer_6_out0, FETCH_2_q,
       IDLE_q, Load, Main, multiplexer_2_out, multiplexer_3_out, multiplexer_4_out, or_1_out, or_5_out,
       or_7_out, or_9_out, or_10_out, or_12_out, or_13_out, or_14_out, Pop, Push, R1, R1_0, R1_1, R1_2, R2_1,
       R3, R3_0, R3_1, R4, R_W_Push, R_W_Store, Store;
  wire [2:0] SS_Code;
  wire [3:0] ALU_OP_t;
  wire [5:0] Func_Code, Op_Code;
  wire [18:0] F_S_Codes, Selector_Codes;

  or or_1 (or_1_out, demultiplexer_1_out1, halt);
  Multiplexer #(.width(4), .enable("false")) multiplexer_1 (.in0(ALU_OP_t), .in1(4'b1000), .out(ALU_Op), .sel(R1));
  or or_2 (R1_0, R1_1, R1_2);
  or or_3 (R3, R3_0, R3_1);
  Demultiplexer #(.enable("false")) demultiplexer_1 (
    .out0(demultiplexer_1_out0), .out1(demultiplexer_1_out1), .in(IDLE_q), .sel(START));
  D_Flip_Flop IDLE (.clk(Clock), .D(or_1_out), .Q(IDLE_q), .preset(START));  // open: Qn, en, reset
  or or_4 (R_W, R_W_Push, R_W_Store);
  Priority_Encoder priority_encoder_1 (
    .in0(1'b1), .in1(R1_0), .in2(CS2), .in3(R3), .in4(R1), .out(SS_Code));  // open: in5, in6, in7, en_in, gs, en_out
  or or_5 (or_5_out, demultiplexer_2_out0, Pop);
  or or_6 (R_W_Push, demultiplexer_3_out0, multiplexer_2_out);
  Multiplexer #(.enable("false")) multiplexer_2 (.in0(Push), .in1(1'b0), .out(multiplexer_2_out), .sel(R2_1));
  // Probe on 19'h6c0a5
  or or_7 (or_7_out, demultiplexer_4_out0, multiplexer_3_out);
  Multiplexer #(.enable("false")) multiplexer_3 (.in0(Load), .in1(1'b0), .out(multiplexer_3_out), .sel(R3));
  or or_8 (R_W_Store, demultiplexer_5_out0, multiplexer_4_out);
  Multiplexer #(.enable("false")) multiplexer_4 (.in0(Store), .in1(1'b0), .out(multiplexer_4_out), .sel(R4));
  or or_9 (or_9_out, demultiplexer_6_out0, CRONORST, demultiplexer_1_out0);
  D_Flip_Flop ReadMemory (.clk(Clock), .D(or_5_out), .Q(CS1));  // open: Qn, preset, en, reset
  D_Flip_Flop WriteMemory (.clk(Clock), .D(R_W_Push), .Q(CS2));  // open: Qn, preset, en, reset
  D_Flip_Flop ReadMemory_2 (.clk(Clock), .D(or_7_out), .Q(CS3));  // open: Qn, preset, en, reset
  D_Flip_Flop WriteMemory_2 (.clk(Clock), .D(R_W_Store), .Q(CS4));  // open: Qn, preset, en, reset
  D_Flip_Flop u_FETCH (.clk(Clock), .D(or_9_out), .Q(CS0), .reset(START));  // open: Qn, preset, en
  Demultiplexer #(.enable("false")) demultiplexer_2 (
    .out0(demultiplexer_2_out0), .out1(R1_1), .in(CS1), .sel(RamReady));
  Demultiplexer #(.enable("false")) demultiplexer_3 (
    .out0(demultiplexer_3_out0), .out1(R2_1), .in(CS2), .sel(RamReady));
  Demultiplexer #(.enable("false")) demultiplexer_4 (
    .out0(demultiplexer_4_out0), .out1(R3_1), .in(CS3), .sel(RamReady));
  Demultiplexer #(.enable("false")) demultiplexer_5 (.out0(demultiplexer_5_out0), .out1(R4), .in(CS4), .sel(RamReady));
  Demultiplexer #(.enable("false")) demultiplexer_6 (
    .out0(demultiplexer_6_out0), .out1(ReadInstruction), .in(CS0), .sel(RamReady));
  Multiplexer #(.select(3), .width(19), .enable("false")) multiplexer_5 (
    .in0(Selector_Codes), .in1(19'h66024), .in2(19'h8010), .in3(19'h6c0a5), .in4(19'h2187), .out(F_S_Codes),
    .sel(SS_Code));  // open: in5, in6, in7
  D_Flip_Flop UpdateStackPointer (.clk(Clock), .D(R1_1), .Q(R1_2));  // open: Qn, preset, en, reset
  D_Flip_Flop save (.clk(Clock), .D(R3_1), .Q(R3_0));  // open: Qn, preset, en, reset
  D_Flip_Flop FETCH_2 (.clk(Clock), .D(ReadInstruction), .Q(FETCH_2_q), .reset(START));  // open: Qn, preset, en
  D_Flip_Flop Add (.clk(Clock), .D(R1_2), .Q(R1));  // open: Qn, preset, en, reset
  or or_10 (or_10_out, CRONORST, CS0);
  or or_11 (ChipSelect, CS4, CS3, CS2, CS1, CS0);
  Multiplexer #(.width(19), .enable("false")) multiplexer_6 (
    .in0(F_S_Codes), .in1({19{1'b0}}), .out(SelectorCodes), .sel(or_10_out));
  Switcher_CU switcher_cu_1 (
    .kbd_rnd(rnd_kbd_Selector), .FuncCode(Func_Code), .OpCode(Op_Code), .ALU_OP(ALU_OP_t),
    .TTY_Enable(TTY_Enable), .halt(halt), .SelectorCodes(Selector_Codes), .S_FC(FC_Selector), .pop(Pop),
    .push(Push), .load(Load), .store(Store), .Main_In(FETCH_2_q), .Main_Out(Main), .kbd_Enable(kbd_Enable));
  Multiplexer #(.width(6), .enable("false")) multiplexer_7 (
    .in0(FuncCode), .in1({6{1'b0}}), .out(Func_Code), .sel(or_12_out));
  or or_12 (or_12_out, R1, CRONORST, R1_0, CS0);
  or or_13 (or_13_out, Main, R4, R3_0, R2_1, R1);
  D_Flip_Flop FETCH_3 (.clk(Clock), .D(or_13_out), .Q(CRONORST), .reset(START));  // open: Qn, preset, en
  Multiplexer #(.width(6), .enable("false")) multiplexer_8 (
    .in0(OpCode), .in1({6{1'b0}}), .out(Op_Code), .sel(or_14_out));
  or or_14 (or_14_out, R1, CRONORST, R1_0, CS0);

  assign fetch = CRONORST;
  assign RESET = START;

  // Other names for the same wires on the sheet: ALU__OP[3:0] = ALU_Op; Chip_Select = ChipSelect; clk = Clock;
  //   Instruction = CRONORST; R2 = CS2; R3_2 = R3_0; ReadIns = ReadInstruction; Selector__Codes[18:0] = SelectorCodes

  // Notes on the sheet:
  //   Input_Output_Region
  //   Instruction-Lines
endmodule
