// Logisim project DataPath.circ as structural Verilog: 1 circuit, main circuit DataPath
module DataPath (
  input  [18:0] Selectors_Code,
  input  [3:0] Op,
  input  kbd_rnd_Selector,
  input  [2:0] S_FlagCondition,
  input  KBD_Enable,
  input  fetch,
  input  reset,
  input  [31:0] MemoryData,
  input  clock,
  input  ReadIns,
  input  [6:0] KBD_Data,
  output [31:0] Memory_Address,
  output [31:0] Memory_Data_Out,
  output [6:0] TTY_Data,
  output [5:0] FuncCode,
  output [5:0] OpCode,
  output KBD_Clear
);

  wire A____B, A____B_t, A___B_signed, A___B_signed_t, A___B_unsigned, FC, not_1_out;
  wire [4:0] DA, Rd, RS, Rt, SA, SB;
  wire [15:0] OffSet;
  wire [25:0] dest;
  wire [27:0] PC;
  wire [31:0] A_prime, ALU_Out, B, B_prime, bit_extender_2_out, Const_extended, DATA_HI, DATA_INPUT, DATA_LO,
       HI, jmp_address, KBD_Data_t, Lo, multiplexer_4_out, NI, random_1_out, Special_Ins_Data;
  wire [31:7] A;
  wire [31:28] final_dest;

  Branch_Control branch_control_1 (
    .JS_Jump_Size(Const_extended), .IA_InstructionAddress({final_dest, PC}), .jmp(Selectors_Code[10]),
    .FC(FC), .NIR_NextInstructionAddrs(NI));
  Multiplexer #(.select(2), .width(5), .enable("false")) multiplexer_1 (
    .in0(Rt), .in1({5{1'b0}}), .in2({5{1'b1}}), .out(SB), .sel(Selectors_Code[4:3]));  // open: in3
  Multiplexer #(.select(2), .width(5), .enable("false")) multiplexer_2 (
    .in0(Rd), .in1(Rt), .in2({5{1'b0}}), .in3({5{1'b1}}), .out(DA), .sel(Selectors_Code[1:0]));
  Multiplexer #(.width(5), .enable("false")) multiplexer_3 (
    .in0(RS), .in1({5{1'b1}}), .out(SA), .sel(Selectors_Code[13]));
  Multiplexer #(.width(32), .enable("false")) multiplexer_4 (
    .in0(Special_Ins_Data), .in1(MemoryData), .out(multiplexer_4_out), .sel(Selectors_Code[17]));
  Multiplexer #(.select(2), .width(32), .enable("false")) multiplexer_5 (
    .in0(ALU_Out), .in1(multiplexer_4_out), .in2(HI), .in3(Lo), .out(DATA_INPUT), .sel(Selectors_Code[6:5]));
  ProgramCounter programcounter_1 (
    .jmp_addr(jmp_address), .jmp_Jump(Selectors_Code[10]), .rst_Reset(reset), .Q({final_dest, PC}),
    .fetch(fetch), .clock(clock));
  assign Const_extended = {{16{OffSet[15]}}, OffSet};  // Bit_Extender bit_extender_1
  Multiplexer #(.width(32), .enable("false")) multiplexer_6 (
    .in0({A, TTY_Data}), .in1({final_dest, dest, 2'b00}), .out(A_prime), .sel(Selectors_Code[18]));
  Multiplexer #(.select(2), .width(32), .enable("false")) multiplexer_7 (
    .in0(B), .in1(Const_extended), .in2({32{1'b0}}), .in3(32'h4), .out(B_prime), .sel(Selectors_Code[8:7]));
  InstructionDecoder instructiondecoder_1 (
    .Instruction(MemoryData), .DA_DataAddress(Rd), .Rs(RS), .Rt(Rt), .dest(dest), .OffSet(OffSet),
    .FuncCode(FuncCode), .OpCode(OpCode), .ReadInstruction(ReadIns));
  not not_1 (not_1_out, A____B_t);
  RegisterFile registerfile_1 (
    .DA_DestinationAddress(DA), .DI_DataInput(DATA_INPUT), .RW_Read_Write(Selectors_Code[2]),
    .Rst_Reset(reset), .SA(SA), .SB(SB), .Out_A({A, TTY_Data}), .Out_B(B), .Clock(clock));
  Multiplexer #(.select(3), .enable("false")) multiplexer_8 (
    .in0(1'b0), .in1(A___B_signed), .in2(A___B_unsigned), .in3(A____B), .in4(A___B_signed_t), .in5(A____B_t),
    .in6(not_1_out), .out(FC), .sel(S_FlagCondition));  // open: in7
  Multiplexer #(.select(2), .width(32), .enable("false")) multiplexer_9 (
    .in0(NI), .in1({A, TTY_Data}), .in2({final_dest, dest, 2'b00}), .in3(ALU_Out), .out(jmp_address),
    .sel(Selectors_Code[12:11]));
  ALU alu_1 (
    .A(A_prime), .B(B_prime), .Op(Op), .HI_CONTENT(DATA_HI), .Output(ALU_Out), .LO_CONTENT(DATA_LO),
    .A___B_unsigned(A___B_unsigned), .A___B_signed(A___B_signed), .A____B(A____B_t), .A____B_2(A____B),
    .A___B_s(A___B_signed_t));
  assign bit_extender_2_out = {{25{1'b0}}, KBD_Data};  // Bit_Extender bit_extender_2
  Random #(.width(32)) random_1 (.clk(clock), .next(1'b1), .out(random_1_out));  // open: clr
  Multiplexer #(.width(32), .enable("false")) multiplexer_10 (
    .in0({32{1'b1}}), .in1(bit_extender_2_out), .out(KBD_Data_t), .sel(KBD_Enable));
  Comparator #(.width(32), .mode("unsigned")) comparator_1 (
    .a(KBD_Data_t), .b({32{1'b1}}), .eq(KBD_Clear));  // open: gt, lt
  Hi_Lo_registers_Finished__main main_1 (
    .HI_Content(DATA_HI), .Lo_Content(DATA_LO), .Update(Selectors_Code[9]), .Reset(reset), .HI_Data(HI),
    .Lo_Data(Lo), .clock(clock));
  Multiplexer #(.width(32), .enable("false")) multiplexer_11 (
    .in0(KBD_Data_t), .in1(random_1_out), .out(Special_Ins_Data), .sel(kbd_rnd_Selector));
  Multiplexer #(.width(32), .enable("false")) multiplexer_12 (
    .in0({A, TTY_Data}), .in1(B), .out(Memory_Data_Out), .sel(Selectors_Code[16]));
  Multiplexer #(.select(2), .width(32), .enable("false")) multiplexer_13 (
    .in0({final_dest, PC}), .in1({A, TTY_Data}), .in2(B), .in3(ALU_Out), .out(Memory_Address),
    .sel(Selectors_Code[15:14]));

  // Other names for the same wires on the sheet: A[6:0] = TTY_Data; clk = clock; final_dest[27:2] = dest;
  //   PC[31:28] = final_dest; KBD_Available = KBD_Enable; MemoryData_MD[31:0] = MemoryData; rst = reset;
  //   S_DA[1:0] = Selectors_Code[1:0]; R_W = Selectors_Code[2]; S_SB[1:0] = Selectors_Code[4:3];
  //   S_DATA_IN[1:0] = Selectors_Code[6:5]; S_ALUB[1:0] = Selectors_Code[8:7]; UpdateHi_Lo = Selectors_Code[9];
  //   Jmp = Selectors_Code[10]; S_jmp_address[1:0] = Selectors_Code[12:11]; S_SA = Selectors_Code[13];
  //   S_Memory_Address[1:0] = Selectors_Code[15:14]; S_MemDataOut = Selectors_Code[16]; S_MD_SI = Selectors_Code[17];
  //   S_ALUA = Selectors_Code[18]

  // Notes on the sheet:
  //   Stack-Pointer
  //   Register File
  //   Stack-Pointer
  //   ALU
  //   DATA PATH
  //   MUX ENTRADAS
  //   Branch Contol
  //   Program Counter
  //   Special Instruction Data Input
  //   Stack-Pointer
  //   Stack-Pointer -4
  //   [RS]
  //   [Rt]
  //   Inputs
  //   Outputs
endmodule
