// Logisim project Hi_Lo_registers(Finished).circ as structural Verilog: 1 circuit, main circuit main
module main (
  input  [31:0] HI_Content,
  input  [31:0] Lo_Content,
  input  Update,
  input  Reset,
  input  Read_HI_Lo,
  output [31:0] HI_Lo_Data
);

  wire clock_1_out;
  wire [31:0] Hi_Register_q, Lo_Register_q;

  Clock clock_1 (.out(clock_1_out));
  Register #(.width(32)) Hi_Register (.D(HI_Content), .en(Update), .Q(Hi_Register_q), .clk(clock_1_out), .clr(Reset));
  Register #(.width(32)) Lo_Register (.D(Lo_Content), .en(Update), .Q(Lo_Register_q), .clk(clock_1_out), .clr(Reset));
  Multiplexer #(.width(32), .enable("false")) multiplexer_1 (
    .in0(Hi_Register_q), .in1(Lo_Register_q), .out(HI_Lo_Data), .sel(Read_HI_Lo));
endmodule
