// Logisim project InstructionDecoder(Finished).circ as structural Verilog: 1 circuit, main circuit InstructionDecoder
module InstructionDecoder (
  input  [31:0] Instruction,
  output [4:0] DA_DataAddress,
  output R_W_ReadWrite,
  output [4:0] SA_SelectorA,
  output [4:0] SB_SelectorB,
  output Jmp,
  output FC_FlagCondition,
  output [25:0] dest,
  output [15:0] A,
  output [3:0] Op,
  output Load,
  output Store,
  output mf_Hi_Lo,
  output [2:0] Op_Type,
  output Read_Hi_Lo,
  output [1:0] EspecialInstruction,
  output Active_EI
);

  wire \and , and_1_out, and_3_out, and_6_out, and_7_out, and_12_out, and_14_out, and_15_out, and_16_out,
       and_17_out, and_18_out, and_19_out, and_20_out, and_21_out, and_22_out, and_23_out, and_24_out,
       and_25_out, and_27_out, and_28_out, and_29_out, and_30_out, and_31_out, and_32_out, and_33_out,
       and_34_out, and_35_out, and_36_out, and_37_out, and_39_out, comparator_1_eq, demultiplexer_3_out0,
       demultiplexer_3_out1, demultiplexer_4_out0, demultiplexer_6_out0, demultiplexer_6_out1,
       demultiplexer_7_out0, demultiplexer_7_out1, div, divu, ds, G_A, G_B, G_C, G_D, G_J, G_Jr, G_L_S,
       G_PoP, ms, mult, multu, \nor , nor_1_out, nor_2_out, nor_3_out, nor_4_out, nor_5_out, nor_6_out,
       nor_7_out, nor_8_out, nor_9_out, nor_10_out, nor_11_out, nor_12_out, nor_13_out, nor_14_out,
       nor_15_out, nor_16_out, nor_17_out, nor_18_out, nor_19_out, nor_20_out, nor_21_out, not_1_out,
       not_2_out, not_3_out, not_4_out, not_5_out, not_6_out, not_7_out, not_8_out, not_9_out, \or ,
       or_4_out, or_7_out, S_A, tunnel, tunnel_t, tunnel_t_t, tunnel_t_t_t, tunnel_t_t_t_t, tunnel_t_t_t_t_t,
       u, \xor ;
  wire [2:0] GroupSelector;
  wire [5:0] S_Code;

  Comparator #(.width(6)) comparator_1 (.a(Instruction[31:26]), .b({6{1'b0}}), .eq(comparator_1_eq));  // open: gt, lt
  not not_1 (not_1_out, Instruction[3]);
  not not_2 (not_2_out, Instruction[5]);
  not not_3 (not_3_out, Instruction[27]);
  not not_4 (not_4_out, Instruction[29]);
  not not_5 (not_5_out, Instruction[30]);
  not not_6 (not_6_out, Instruction[31]);
  nor nor_1 (nor_1_out, G_C, G_J, G_D);
  not not_7 (not_7_out, Instruction[26]);
  not not_8 (not_8_out, G_Jr);
  not not_9 (not_9_out, and_1_out);
  and and_1 (and_1_out, not_1_out, Instruction[4], not_2_out);
  // OR_Gate or_1 has open pins: in0=Instruction[0], in1=Instruction[1], in2=Instruction[2], in3=Instruction[4], in4=Instruction[5], out=open
  nor nor_2 (nor_2_out, Instruction[0], Instruction[1], Instruction[2], Instruction[4], Instruction[5]);
  and and_2 (G_J, Instruction[27], nor_3_out);
  nor nor_3 (nor_3_out, Instruction[26], Instruction[28], Instruction[29], Instruction[30], Instruction[31]);
  // OR_Gate or_2 has open pins: in0=Instruction[26], in1=Instruction[28], in2=Instruction[29], in3=Instruction[30], in4=Instruction[31], out=open
  and and_3 (and_3_out, Instruction[26], nor_4_out);
  // OR_Gate or_3 has open pins: in0=Instruction[27], in1=Instruction[28], in2=Instruction[29], in3=Instruction[30], in4=Instruction[31], out=open
  nor nor_4 (nor_4_out, Instruction[27], Instruction[28], Instruction[29], Instruction[30], Instruction[31]);
  or or_4 (or_4_out, Instruction[26], Instruction[27], Instruction[28], Instruction[29]);
  nor nor_5 (nor_5_out, Instruction[30], Instruction[31]);
  and and_4 (G_PoP, not_7_out, Instruction[30], Instruction[31]);
  and and_5 (Active_EI, Instruction[26], Instruction[30], Instruction[31]);
  Demultiplexer demultiplexer_1 (.out0(Load), .out1(Store), .in(1'b1), .sel(Instruction[29]), .en(and_7_out));
  and and_6 (and_6_out, Instruction[26], Instruction[27], Instruction[31]);
  and and_7 (and_7_out, and_6_out, nor_6_out);
  nor nor_6 (nor_6_out, Instruction[28], Instruction[30]);
  and and_8 (G_A, comparator_1_eq, not_8_out, not_9_out);
  and and_9 (mf_Hi_Lo, comparator_1_eq, and_1_out);
  and and_10 (G_Jr, nor_2_out, comparator_1_eq, Instruction[3]);
  and and_11 (G_C, not_3_out, Instruction[28], not_4_out, not_5_out, not_6_out);
  and and_12 (and_12_out, Instruction[27], Instruction[28], not_4_out, not_5_out, not_6_out);
  or or_5 (G_D, and_12_out, and_3_out);
  and and_13 (G_B, or_4_out, nor_5_out, nor_1_out);
  or or_6 (G_L_S, Load, Store);
  or or_7 (or_7_out, Active_EI, G_A, G_PoP);
  Priority_Encoder priority_encoder_1 (
    .in0(or_7_out), .in1(G_B), .in2(G_C), .in3(G_D), .in4(mf_Hi_Lo), .in5(G_J), .in6(G_Jr), .in7(G_L_S),
    .out(GroupSelector));  // open: en_in, gs, en_out
  Multiplexer #(.select(3), .width(8), .enable("false")) multiplexer_1 (
    .in0({8{1'b0}}), .in1(8'h45), .in2(8'h52), .in3(8'he), .in4(8'h80), .in5(8'h3e), .in6(8'h1c), .in7(8'h5),
    .out({R_W_ReadWrite, S_A, S_Code[5], FC_FlagCondition, Jmp, S_Code[2:0]}), .sel(GroupSelector));
  Priority_Encoder priority_encoder_2 (
    .in0(G_A), .in1(G_B), .in2(G_C), .in3(G_D), .in4(mf_Hi_Lo), .in5(G_PoP), .in6(Active_EI), .in7(G_L_S),
    .out(Op_Type));  // open: en_in, gs, en_out
  Multiplexer #(.select(2), .width(5), .enable("false")) multiplexer_2 (
    .in0(Instruction[15:11]), .in1(Instruction[20:16]), .in2({5{1'b0}}), .out(DA_DataAddress),
    .sel(S_Code[1:0]));  // open: in3
  Multiplexer #(.width(5), .enable("false")) multiplexer_3 (
    .in0(Instruction[20:16]), .in1({5{1'b0}}), .out(SB_SelectorB), .sel(S_Code[2]));
  Multiplexer #(.width(26), .enable("false")) multiplexer_4 (
    .in0({26{1'b0}}), .in1(Instruction[25:0]), .out(dest), .sel(S_Code[5]));
  Multiplexer #(.width(16), .enable("false")) multiplexer_5 (
    .in0({16{1'b0}}), .in1(Instruction[15:0]), .out(A), .sel(S_A));
  and and_14 (and_14_out, Instruction[27], Instruction[29]);
  and and_15 (and_15_out, Instruction[0], Instruction[2], Instruction[4]);
  nor nor_7 (nor_7_out, Instruction[28], Instruction[30], Instruction[31]);
  and and_16 (and_16_out, Instruction[26], Instruction[27], Instruction[29]);
  and and_17 (and_17_out, Instruction[0], Instruction[1], Instruction[3], Instruction[5]);
  nor nor_8 (nor_8_out, Instruction[2], Instruction[4]);
  and and_18 (and_18_out, Instruction[27], Instruction[28]);
  and and_19 (and_19_out, and_18_out, nor_9_out);
  nor nor_9 (nor_9_out, Instruction[29], Instruction[30], Instruction[31]);
  nor nor_10 (nor_10_out, Instruction[27], Instruction[29], Instruction[30], Instruction[31]);
  nor nor_11 (nor_11_out, Instruction[0], Instruction[2], Instruction[3], Instruction[4]);
  and and_20 (and_20_out, Instruction[26], nor_12_out);
  nor nor_12 (nor_12_out, Instruction[27], Instruction[28], Instruction[29], Instruction[30], Instruction[31]);
  nor nor_13 (nor_13_out, Instruction[26], Instruction[28], Instruction[30], Instruction[31]);
  and and_21 (and_21_out, nor_13_out, and_14_out);
  nor nor_14 (nor_14_out, Instruction[1], Instruction[3], Instruction[5]);
  and and_22 (and_22_out, nor_14_out, and_15_out);
  and and_23 (and_23_out, nor_7_out, and_16_out);
  and and_24 (and_24_out, and_17_out, nor_8_out);
  Demultiplexer demultiplexer_2 (
    .out0(tunnel_t_t_t), .out1(tunnel_t_t_t_t_t), .in(1'b1), .sel(Instruction[26]), .en(and_19_out));
  Demultiplexer demultiplexer_3 (
    .out0(demultiplexer_3_out0), .out1(demultiplexer_3_out1), .in(1'b1), .sel(Instruction[26]),
    .en(and_25_out));
  and and_25 (and_25_out, Instruction[28], nor_10_out);
  Demultiplexer demultiplexer_4 (
    .out0(demultiplexer_4_out0), .out1(tunnel_t), .in(1'b1), .sel(Instruction[1]), .en(Instruction[1]));
  and and_26 (Instruction[1], nor_11_out, Instruction[5]);
  nor nor_15 (nor_15_out, Instruction[26], Instruction[27], Instruction[28], Instruction[30], Instruction[31]);
  and and_27 (and_27_out, nor_15_out, Instruction[29]);
  or or_8 (tunnel_t_t, and_20_out, and_21_out, and_22_out);
  or or_9 (u, and_23_out, and_24_out);
  or or_10 (tunnel_t_t_t_t, demultiplexer_3_out0, demultiplexer_3_out1);
  or or_11 (tunnel, demultiplexer_4_out0, and_27_out);
  Demultiplexer #(.enable("false")) demultiplexer_5 (.out0(ms), .out1(ds), .in(1'b1), .sel(Instruction[1]));
  nor nor_16 (nor_16_out, Instruction[2], Instruction[5]);
  and and_28 (and_28_out, Instruction[3], Instruction[4]);
  Demultiplexer demultiplexer_6 (
    .out0(demultiplexer_6_out0), .out1(demultiplexer_6_out1), .in(1'b1), .sel(Instruction[0]), .en(and_29_out));
  nor nor_17 (nor_17_out, Instruction[1], Instruction[3], Instruction[4]);
  and and_29 (and_29_out, nor_17_out, and_30_out);
  and and_30 (and_30_out, Instruction[2], Instruction[5]);
  Demultiplexer demultiplexer_7 (
    .out0(demultiplexer_7_out0), .out1(demultiplexer_7_out1), .in(1'b1), .sel(Instruction[26]),
    .en(and_31_out));
  nor nor_18 (nor_18_out, Instruction[27], Instruction[30], Instruction[31]);
  and and_31 (and_31_out, nor_18_out, and_32_out);
  and and_32 (and_32_out, Instruction[28], Instruction[29]);
  and and_33 (and_33_out, Instruction[0], Instruction[1], Instruction[2], Instruction[5]);
  nor nor_19 (nor_19_out, Instruction[3], Instruction[4]);
  nor nor_20 (nor_20_out, Instruction[0], Instruction[1], Instruction[2], Instruction[4]);
  and and_34 (and_34_out, Instruction[3], Instruction[5]);
  and and_35 (and_35_out, Instruction[27], Instruction[28], Instruction[29]);
  and and_36 (and_36_out, and_35_out, nor_21_out);
  nor nor_21 (nor_21_out, Instruction[26], Instruction[30], Instruction[31]);
  // Priority_Encoder #(.select(4)) priority_encoder_3: pin names not known; wires that end beside it: 1'b0, tunnel_t_t_t_t_t, tunnel_t_t_t, tunnel_t_t_t_t, mult, multu, div, divu, Op, tunnel, tunnel_t, \and , \or , \nor , \xor , tunnel_t_t, u
  Demultiplexer demultiplexer_8 (.out0(div), .out1(divu), .in(ds), .sel(Instruction[0]), .en(and_37_out));
  and and_37 (and_37_out, nor_16_out, and_28_out);
  Demultiplexer demultiplexer_9 (.out0(mult), .out1(multu), .in(ms), .sel(Instruction[0]), .en(and_37_out));
  and and_38 (\nor , and_33_out, nor_19_out);
  and and_39 (and_39_out, nor_20_out, and_34_out);
  or or_12 (\xor , and_39_out, and_36_out);
  or or_13 (\and , demultiplexer_6_out0, demultiplexer_7_out0);
  or or_14 (\or , demultiplexer_6_out1, demultiplexer_7_out1);

  assign EspecialInstruction = Instruction[1:0];
  assign Read_Hi_Lo = Instruction[1];
  assign SA_SelectorA = Instruction[25:21];

  // Other names for the same wires on the sheet: DA[4:0] = DA_DataAddress; G_E = mf_Hi_Lo; G_EI = Active_EI;
  //   EI_Selector[1:0] = Instruction[1:0]; FuncCode[5:0] = Instruction[5:0]; Inst[31:0] = Instruction;
  //   X[4:0] = Instruction[10:6]; RD[4:0] = Instruction[15:11]; Rt[4:0] = Instruction[20:16];
  //   Rs[4:0] = Instruction[25:21]; OpCode[5:0] = Instruction[31:26]; Lw = Load; S_DA[1:0] = S_Code[1:0];
  //   S_Sb = S_Code[2]; S_Code (some bits) = {R_W_ReadWrite, S_A, FC_FlagCondition, Jmp}; FC = FC_FlagCondition;
  //   S_dest = S_Code[5]; R_W = R_W_ReadWrite; SB[4:0] = SB_SelectorB; Sw = Store

  // Notes on the sheet:
  //   Input_Otput_Region
  //   FuncCode
  //   OP-Code
  //   Decodificacion_por_grupo
  //   Pop_Push
  //   Especial_Ins
  //   RD
  //   Rt
  //   Rs
  //   Group_A
  //   Group_E
  //   Group_J
  //   Group_C
  //   Group_D
  //   Group_B
  //   Mapeo_Grupo_Selector
  //   Mux_Salidas
  //   Mapeo_Func_ALUCODE
endmodule
