// Logisim project InstructionMemory(Finished).circ as structural Verilog: 1 circuit, main circuit InstructionMemory
module InstructionMemory (
  input  [31:0] PC_ProgramCounter,
  input  fetch,
  input  [31:0] Word,
  input  upd_InstructionUpdated,
  input  rst_reset,
  output [15:0] addrs,
  output [3:0] mask,
  output R_W,
  output Chip_Select,
  output [31:0] Instruction,
  output fetched
);

  wire and_1_out, clk;

  Clock u_clk (.out(clk));
  and and_1 (and_1_out, fetch, upd_InstructionUpdated);
  Register #(.width(32)) Instruction_Register (.D(Word), .en(and_1_out), .Q(Instruction), .clk(clk), .clr(rst_reset));
  Decoder #(.select(2), .enable("false")) decoder_1 (
    .out0(mask[0]), .out1(mask[1]), .out2(mask[2]), .out3(mask[3]), .sel(PC_ProgramCounter[3:2]));
  not not_1 (R_W, fetch);
  and and_2 (fetched, fetch, clk, upd_InstructionUpdated);

  assign addrs = PC_ProgramCounter[19:4];
  assign Chip_Select = fetch;

  // Other names for the same wires on the sheet: Inst[31:0] = Instruction; mask_t[1:0] = PC_ProgramCounter[3:2];
  //   rst = rst_reset; upd = upd_InstructionUpdated
endmodule
