// Logisim project Memory_Controller(Finished).circ as structural Verilog: 2 circuits, main circuit Memory Controller
module Memory_Controller (
  input  [31:0] MemoryAddress,
  input  [31:0] Input_Word,
  input  [31:0] O0,
  input  [31:0] O1,
  input  [31:0] O2,
  input  [31:0] O3,
  input  R_W,
  input  Chip_Select,
  input  [3:0] Read_Time,
  input  [3:0] Write_Time,
  input  reset,
  input  clk,
  input  GENERAL_RST,
  output [15:0] Address,
  output [31:0] OW_Out_Word,
  output [3:0] Mask,
  output [31:0] I0,
  output [31:0] I1,
  output [31:0] I2,
  output [31:0] I3,
  output Ram_Ready
);

  wire M0_prime, M1_prime, M2_prime, M3_prime, S0, S1, S2, S3;
  wire [3:0] multiplexer_2_out;
  wire [31:0] multiplexer_3_out, multiplexer_5_out, multiplexer_7_out, O0_t, O1_t, O2_t, O3_t;

  Register #(.width(32), .trigger("high")) register_1 (
    .D(O0), .en(Chip_Select), .Q(O0_t), .clk(clk), .clr(GENERAL_RST));
  Register #(.width(32), .trigger("high")) register_2 (
    .D(O1), .en(Chip_Select), .Q(O1_t), .clk(clk), .clr(GENERAL_RST));
  Register #(.width(32), .trigger("high")) register_3 (
    .D(O2), .en(Chip_Select), .Q(O2_t), .clk(clk), .clr(GENERAL_RST));
  Register #(.width(32), .trigger("high")) register_4 (
    .D(O3), .en(Chip_Select), .Q(O3_t), .clk(clk), .clr(GENERAL_RST));
  Decoder #(.select(2), .enable("false")) decoder_1 (
    .out0(Mask[0]), .out1(Mask[1]), .out2(Mask[2]), .out3(Mask[3]), .sel(MemoryAddress[3:2]));
  Multiplexer #(.width(32), .enable("false")) multiplexer_1 (
    .in0(O0_t), .in1({Input_Word[7:0], Input_Word[15:8], Input_Word[23:16], Input_Word[31:24]}), .out(I0),
    .sel(S0));
  Multiplexer #(.width(4), .disabled(0), .enable("false")) multiplexer_2 (
    .in0(Read_Time), .in1(Write_Time), .out(multiplexer_2_out), .sel(R_W));
  Multiplexer #(.width(32), .enable("false")) multiplexer_3 (
    .in0({32{1'b0}}), .in1(O0_t), .out(multiplexer_3_out), .sel(M0_prime));
  Multiplexer #(.width(32), .enable("false")) multiplexer_4 (
    .in0(O1_t), .in1({Input_Word[7:0], Input_Word[15:8], Input_Word[23:16], Input_Word[31:24]}), .out(I1),
    .sel(S1));
  and and_1 (S0, R_W, Mask[0], Chip_Select);
  and and_2 (S2, R_W, Mask[2], Chip_Select);
  Multiplexer #(.width(32), .enable("false")) multiplexer_5 (
    .in0(multiplexer_3_out), .in1(O1_t), .out(multiplexer_5_out), .sel(M1_prime));
  Multiplexer #(.width(32), .enable("false")) multiplexer_6 (
    .in0(O2_t), .in1({Input_Word[7:0], Input_Word[15:8], Input_Word[23:16], Input_Word[31:24]}), .out(I2),
    .sel(S2));
  Chronometer chronometer_1 (
    .WaitTime(multiplexer_2_out), .ChipSelect(Chip_Select), .Clock(clk), .Reset(reset), .Ready(Ram_Ready));
  Multiplexer #(.width(32), .enable("false")) multiplexer_7 (
    .in0(multiplexer_5_out), .in1(O2_t), .out(multiplexer_7_out), .sel(M2_prime));
  and and_3 (S1, R_W, Mask[1], Chip_Select);
  and and_4 (S3, R_W, Mask[3], Chip_Select);
  // Probe on {OW_Out_Word[7:0], OW_Out_Word[15:8], OW_Out_Word[23:16], OW_Out_Word[31:24]}
  Multiplexer #(.width(32), .enable("false")) multiplexer_8 (
    .in0(multiplexer_7_out), .in1(O3_t),
    .out({OW_Out_Word[7:0], OW_Out_Word[15:8], OW_Out_Word[23:16], OW_Out_Word[31:24]}), .sel(M3_prime));
  Multiplexer #(.width(32), .enable("false")) multiplexer_9 (
    .in0(O3_t), .in1({Input_Word[7:0], Input_Word[15:8], Input_Word[23:16], Input_Word[31:24]}), .out(I3),
    .sel(S3));
  and and_5 (M0_prime, Mask[0], Ram_Ready);
  and and_6 (M1_prime, Mask[1], Ram_Ready);
  and and_7 (M2_prime, Mask[2], Ram_Ready);
  and and_8 (M3_prime, Mask[3], Ram_Ready);

  assign Address = MemoryAddress[19:4];

  // Other names for the same wires on the sheet: M0 = Mask[0]; M1 = Mask[1]; M2 = Mask[2]; M3 = Mask[3];
  //   decode_mask[1:0] = MemoryAddress[3:2]; reset_t = GENERAL_RST; resetch = reset; RT[3:0] = Read_Time;
  //   Upd = Ram_Ready; Win[31:0] = {Input_Word[7:0], Input_Word[15:8], Input_Word[23:16], Input_Word[31:24]};
  //   Win_prime[31:0] = Input_Word; Wout[31:0] = OW_Out_Word;
  //   Wout_prime[31:0] = {OW_Out_Word[7:0], OW_Out_Word[15:8], OW_Out_Word[23:16], OW_Out_Word[31:24]};
  //   WT[3:0] = Write_Time

  // Notes on the sheet:
  //   Input/Output_Region
  //   Mask-Decoder
  //   Counter
  //   Read_BankSelector
  //   Write_BankSelector
endmodule

module Chronometer (
  input  [3:0] WaitTime,
  input  ChipSelect,
  input  Reset,
  input  Clock,
  output Ready
);

  wire counter_1_carry;

  Counter #(.width(4), .max('hf), .ongoal("load")) counter_1 (
    .load(1'b1), .D(WaitTime), .count(ChipSelect), .carry(counter_1_carry), .clk(Clock));  // open: Q, clr
  D_Flip_Flop #(.trigger("falling")) d_ff_1 (
    .clk(Clock), .D(counter_1_carry), .Q(Ready), .reset(Reset));  // open: Qn, preset, en

  // Other names for the same wires on the sheet: clk = Clock
endmodule
