// Logisim project Memory_Controller.circ as structural Verilog
// Chip Selector
module Memory_Controller (
  input  [15:0] Address,
  input  [3:0] Mask,
  input  [31:0] O0,
  input  [31:0] O2,
  input  [31:0] Read_Time,
  input  R_W,
  input  Chip_Selector,
  input  [31:0] Input_Word,
  input  [31:0] O1,
  input  [31:0] O3,
  input  [31:0] Write_Time,
  output [31:0] OW,
  output Ready,
  output CS,
  output [3:0] Mask_2,
  output R_W_2,
  output [31:0] OW_2,
  output [15:0] Address_2
);

  wire clock_1_out;
  wire [31:0] Time;

  Multiplexer #(.width(32)) multiplexer_1 (
    .in0(Read_Time), .in1(Write_Time), .out(Time), .sel(R_W), .en(Chip_Selector));
  Clock clock_1 (.out(clock_1_out));
  Counter #(.width(32), .max('hffffffff)) counter_1 (
    .load(1'b1), .D(Time), .count(1'b1), .carry(Ready), .clk(clock_1_out));  // open: Q, clr

  assign Address_2 = Address;
  assign CS = Chip_Selector;
  assign Mask_2 = Mask;
  assign OW_2 = Input_Word;
  assign R_W_2 = R_W;

  // Other names for the same wires on the sheet: RT[31:0] = Read_Time; Word[31:0] = Input_Word; WT[31:0] = Write_Time

  // Notes on the sheet:
  //   Control Unit inputs
  //   Select Time
  //   Ram Inputs
  //   Counter
  //   Ram Outputs
endmodule

module borrar (
  output [2:0] out_1
);

  wire clock_1_out;

  Clock clock_1 (.out(clock_1_out));
  Counter #(.width(3), .max('h7)) counter_1 (
    .load(1'b1), .D(3'b111), .count(1'b1), .Q(out_1), .clk(clock_1_out));  // open: carry, clr
  // Probe on nothing
endmodule
