// Logisim project Special_Ops_Unit(Finished).circ as structural Verilog: 1 circuit, main circuit Special_Op_Unit
module Special_Op_Unit (
  input  Enable,
  input  [1:0] EspIns_Selector,
  input  [31:0] RS_Data,
  input  [6:0] KBD_Data,
  input  KBD_Enable,
  output Halt,
  output [6:0] TTY_DATA,
  output TTY_Enable,
  output Write_Data,
  output [31:0] RD_Data
);

  wire clock_1_out, kbd_t, rnd;
  wire [31:0] bit_extender_1_out, multiplexer_1_out, rnd_out;

  Decoder #(.select(2)) decoder_1 (
    .out0(kbd_t), .out1(TTY_Enable), .out2(rnd), .out3(Halt), .sel(EspIns_Selector), .en(Enable));
  or or_1 (Write_Data, kbd_t, rnd);
  Clock clock_1 (.out(clock_1_out));
  assign bit_extender_1_out = {{25{1'b0}}, KBD_Data};  // Bit_Extender bit_extender_1
  Random #(.width(32)) u_rnd (.clk(clock_1_out), .next(rnd), .out(rnd_out));  // open: clr
  Multiplexer #(.width(32)) multiplexer_1 (
    .in0({32{1'b1}}), .in1(bit_extender_1_out), .out(multiplexer_1_out), .sel(KBD_Enable), .en(kbd_t));
  Multiplexer #(.width(32)) multiplexer_2 (
    .in0(multiplexer_1_out), .in1(rnd_out), .out(RD_Data), .sel(EspIns_Selector[1]), .en(Write_Data));

  assign TTY_DATA = RS_Data[6:0];

  // Other names for the same wires on the sheet: EI_S[1:0] = EspIns_Selector; KBD[6:0] = KBD_Data;
  //   KBD_EN = KBD_Enable; RS[31:0] = RS_Data; tty = TTY_Enable; Write = Write_Data
endmodule
