// Logisim project Switcher_CU.circ as structural Verilog: 1 circuit, main circuit Switcher-CU
module Switcher_CU (
  input  [5:0] FuncCode,
  input  [5:0] OpCode,
  input  Main_In,
  output [18:0] SelectorCodes,
  output [3:0] ALU_OP,
  output [2:0] S_FC,
  output pop,
  output push,
  output load,
  output store,
  output Main_Out,
  output kbd_Enable,
  output kbd_rnd,
  output TTY_Enable,
  output halt
);

  wire \and , and_2_out, and_4_out, and_5_out, and_7_out, and_8_out, and_9_out, and_10_out, and_15_out,
       and_22_out, and_23_out, and_24_out, and_25_out, and_26_out, and_27_out, and_28_out, and_29_out,
       and_30_out, and_31_out, and_32_out, and_33_out, and_34_out, and_35_out, and_36_out, and_37_out,
       and_38_out, and_39_out, and_40_out, and_41_out, and_42_out, and_43_out, and_44_out, and_45_out,
       and_47_out, and_48_out, and_49_out, comparator_1_eq, demultiplexer_7_out0, demultiplexer_7_out1,
       demultiplexer_11_out0, demultiplexer_11_out1, demultiplexer_12_out0, demultiplexer_12_out1, div, divu,
       ds, G_A, G_Aritmet, G_B, G_C, G_D, G_E, G_EI, G_J, G_Jr, G_L_S, Hi, kbd_rnd_t, Low, ms, mult,
       Mult_Div, multu, nop, \nor , nor_1_out, nor_2_out, nor_3_out, nor_4_out, nor_5_out, nor_6_out,
       nor_7_out, nor_8_out, nor_10_out, nor_11_out, nor_12_out, nor_13_out, nor_14_out, nor_15_out,
       nor_16_out, nor_17_out, nor_18_out, nor_19_out, nor_20_out, nor_21_out, nor_22_out, nor_23_out,
       nor_24_out, nor_25_out, not_1_out, not_2_out, not_3_out, not_4_out, not_5_out, not_6_out, not_7_out,
       not_8_out, not_9_out, not_10_out, not_11_out, not_12_out, not_13_out, not_FC, \or , or_4_out,
       or_5_out, or_8_out, PopStLd, tunnel, tunnel_t, tunnel_t_t, tunnel_t_t_t, tunnel_t_t_t_t,
       tunnel_t_t_t_t_t, tunnel_t_t_t_t_t_t, u, \xor ;
  wire [3:0] G_Selector;

  Demultiplexer #(.enable("false")) demultiplexer_1 (.out0(Low), .out1(Hi), .in(G_E), .sel(FuncCode[1]));
  nor nor_1 (nor_1_out, halt, pop, push, load, store);
  Comparator #(.width(6)) comparator_1 (.a(OpCode), .b({6{1'b0}}), .eq(comparator_1_eq));  // open: gt, lt
  not not_1 (not_1_out, FuncCode[3]);
  not not_2 (not_2_out, FuncCode[5]);
  not not_3 (not_3_out, OpCode[1]);
  not not_4 (not_4_out, OpCode[3]);
  not not_5 (not_5_out, OpCode[4]);
  not not_6 (not_6_out, OpCode[5]);
  nor nor_2 (nor_2_out, G_C, G_J, G_D);
  not not_7 (not_7_out, OpCode[0]);
  and and_1 (Main_Out, Main_In, nor_1_out);
  not not_8 (not_8_out, G_Jr);
  not not_9 (not_9_out, and_2_out);
  and and_2 (and_2_out, not_1_out, FuncCode[4], not_2_out);
  // OR_Gate or_1 has open pins: in0=FuncCode[0], in1=FuncCode[1], in2=FuncCode[2], in3=FuncCode[4], in4=FuncCode[5], out=open
  nor nor_3 (nor_3_out, FuncCode[0], FuncCode[1], FuncCode[2], FuncCode[4], FuncCode[5]);
  and and_3 (G_J, OpCode[1], nor_4_out);
  // OR_Gate or_2 has open pins: in0=OpCode[0], in1=OpCode[2], in2=OpCode[3], in3=OpCode[4], in4=OpCode[5], out=open
  nor nor_4 (nor_4_out, OpCode[0], OpCode[2], OpCode[3], OpCode[4], OpCode[5]);
  and and_4 (and_4_out, OpCode[0], nor_5_out);
  nor nor_5 (nor_5_out, OpCode[1], OpCode[2], OpCode[3], OpCode[4], OpCode[5]);
  // OR_Gate or_3 has open pins: in0=OpCode[1], in1=OpCode[2], in2=OpCode[3], in3=OpCode[4], in4=OpCode[5], out=open
  or or_4 (or_4_out, OpCode[0], OpCode[1], OpCode[2], OpCode[3]);
  nor nor_6 (nor_6_out, OpCode[4], OpCode[5]);
  and and_5 (and_5_out, not_7_out, OpCode[4], OpCode[5]);
  and and_6 (G_EI, OpCode[0], OpCode[4], OpCode[5]);
  and and_7 (and_7_out, OpCode[0], OpCode[1], OpCode[5]);
  and and_8 (and_8_out, and_7_out, nor_7_out);
  nor nor_7 (nor_7_out, OpCode[2], OpCode[4]);
  nor nor_8 (nor_8_out, div, divu, mult, multu);
  or or_5 (or_5_out, div, divu, mult, multu);
  not not_10 (not_10_out, FuncCode[0]);
  and and_9 (and_9_out, not_10_out, not_11_out);
  not not_11 (not_11_out, FuncCode[1]);
  and and_10 (and_10_out, FuncCode[1], not_12_out);
  not not_12 (not_12_out, FuncCode[0]);
  Demultiplexer #(.select(2), .enable("false")) demultiplexer_2 (
    .out1(TTY_Enable), .out3(halt), .in(G_EI), .sel(FuncCode[1:0]));  // open: out0, out2
  and and_11 (G_A, comparator_1_eq, not_8_out, not_9_out);
  and and_12 (G_E, comparator_1_eq, and_2_out);
  and and_13 (G_Jr, nor_3_out, comparator_1_eq, FuncCode[3]);
  and and_14 (G_C, not_3_out, OpCode[2], not_4_out, not_5_out, not_6_out);
  and and_15 (and_15_out, OpCode[1], OpCode[2], not_4_out, not_5_out, not_6_out);
  or or_6 (G_D, and_15_out, and_4_out);
  and and_16 (G_B, or_4_out, nor_6_out, nor_2_out);
  Demultiplexer #(.enable("false")) demultiplexer_3 (.out0(pop), .out1(push), .in(and_5_out), .sel(FuncCode[0]));
  Demultiplexer #(.enable("false")) demultiplexer_4 (.out0(load), .out1(store), .in(and_8_out), .sel(OpCode[3]));
  or or_7 (G_L_S, load, store);
  and and_17 (G_Aritmet, nor_8_out, G_A);
  and and_18 (Mult_Div, or_5_out, G_A);
  or or_8 (or_8_out, and_9_out, and_10_out);
  and and_19 (kbd_Enable, G_EI, not_13_out);
  not not_13 (not_13_out, kbd_rnd_t);
  and and_20 (kbd_rnd_t, G_EI, or_8_out);
  Multiplexer #(.select(4), .width(19), .enable("false")) multiplexer_1 (
    .in0(19'h4), .in1(19'h204), .in2(19'h8d), .in3(19'h402), .in4(19'h502), .in5(19'h2c), .in6(19'ha),
    .in7(19'h4c), .in8(19'h6c), .in9(19'h1d80), .in10(19'h41d80), .in11(19'h6000), .in12(19'h2187),
    .in13(19'h1c080), .in14(19'hc080), .out(SelectorCodes), .sel(G_Selector));  // open: in15
  Priority_Encoder #(.select(4)) priority_encoder_1 (
    .in0(G_Aritmet), .in1(Mult_Div), .in2(G_B), .in3(G_C), .in4(G_D), .in5(kbd_rnd_t), .in6(TTY_Enable),
    .in7(Low), .in8(Hi), .in9(G_Jr), .in10(G_J), .in11(pop), .in12(push), .in13(store), .in14(load),
    .out(G_Selector));  // open: in15, gs, en_out, en_in
  Priority_Encoder priority_encoder_2 (
    .in0(not_FC), .in1(tunnel_t_t_t), .in2(u), .in3(tunnel_t_t_t_t), .in4(tunnel_t_t_t_t_t_t),
    .in5(tunnel_t_t_t_t_t), .in6(tunnel), .out(S_FC));  // open: in7, en_in, gs, en_out
  nor nor_9 (not_FC, tunnel_t_t_t, tunnel_t_t_t_t, tunnel_t_t_t_t_t, u, tunnel_t_t_t_t_t_t);
  nor nor_10 (nor_10_out, FuncCode[0], FuncCode[1], FuncCode[2], FuncCode[3], FuncCode[4], FuncCode[5]);
  and and_21 (nop, G_A, nor_10_out);
  or or_9 (PopStLd, G_L_S, pop);
  and and_22 (and_22_out, OpCode[1], OpCode[3]);
  and and_23 (and_23_out, FuncCode[1], FuncCode[3], FuncCode[5]);
  nor nor_11 (nor_11_out, FuncCode[0], FuncCode[2], FuncCode[4]);
  nor nor_12 (nor_12_out, OpCode[2], OpCode[4], OpCode[5]);
  and and_24 (and_24_out, OpCode[0], OpCode[1], OpCode[3]);
  and and_25 (and_25_out, FuncCode[0], FuncCode[1], FuncCode[3], FuncCode[5]);
  nor nor_13 (nor_13_out, FuncCode[2], FuncCode[4]);
  and and_26 (and_26_out, OpCode[1], OpCode[2]);
  and and_27 (and_27_out, and_26_out, nor_14_out);
  nor nor_14 (nor_14_out, OpCode[3], OpCode[4], OpCode[5]);
  nor nor_15 (nor_15_out, OpCode[1], OpCode[3], OpCode[4], OpCode[5]);
  nor nor_16 (nor_16_out, FuncCode[0], FuncCode[2], FuncCode[3], FuncCode[4]);
  and and_28 (and_28_out, OpCode[0], nor_17_out);
  nor nor_17 (nor_17_out, OpCode[1], OpCode[2], OpCode[3], OpCode[4], OpCode[5]);
  nor nor_18 (nor_18_out, OpCode[0], OpCode[2], OpCode[4], OpCode[5]);
  and and_29 (and_29_out, nor_18_out, and_22_out);
  and and_30 (and_30_out, and_23_out, nor_11_out);
  and and_31 (and_31_out, nor_12_out, and_24_out);
  and and_32 (and_32_out, and_25_out, nor_13_out);
  Demultiplexer #(.enable("false")) demultiplexer_5 (
    .out0(tunnel_t_t_t_t), .out1(tunnel_t_t_t_t_t_t), .in(and_27_out), .sel(OpCode[0]));
  Demultiplexer #(.enable("false")) demultiplexer_6 (
    .out0(tunnel_t_t_t_t_t), .out1(tunnel), .in(and_33_out), .sel(OpCode[0]));
  and and_33 (and_33_out, OpCode[2], nor_15_out);
  Demultiplexer #(.enable("false")) demultiplexer_7 (
    .out0(demultiplexer_7_out0), .out1(demultiplexer_7_out1), .in(and_34_out), .sel(FuncCode[1]));
  and and_34 (and_34_out, nor_16_out, FuncCode[5]);
  nor nor_19 (nor_19_out, OpCode[0], OpCode[1], OpCode[2], OpCode[4], OpCode[5]);
  and and_35 (and_35_out, nor_19_out, OpCode[3]);
  or or_10 (tunnel_t_t_t, and_28_out, and_29_out, and_30_out);
  or or_11 (u, and_31_out, and_32_out);
  or or_12 (tunnel_t, demultiplexer_7_out0, PopStLd, and_35_out);
  or or_13 (tunnel_t_t, G_J, push, G_Jr, demultiplexer_7_out1);
  Demultiplexer #(.enable("false")) demultiplexer_8 (.out0(ms), .out1(ds), .in(1'b1), .sel(FuncCode[1]));
  nor nor_20 (nor_20_out, FuncCode[2], FuncCode[5]);
  and and_36 (and_36_out, FuncCode[3], G_A, FuncCode[4]);
  nor nor_21 (nor_21_out, FuncCode[1], FuncCode[3], FuncCode[4]);
  and and_37 (and_37_out, nor_21_out, and_38_out);
  and and_38 (and_38_out, FuncCode[2], FuncCode[5]);
  nor nor_22 (nor_22_out, OpCode[1], OpCode[4], OpCode[5]);
  and and_39 (and_39_out, nor_22_out, and_40_out);
  and and_40 (and_40_out, OpCode[2], OpCode[3]);
  and and_41 (and_41_out, FuncCode[0], FuncCode[1], FuncCode[2], FuncCode[5]);
  nor nor_23 (nor_23_out, FuncCode[3], FuncCode[4]);
  nor nor_24 (nor_24_out, FuncCode[0], FuncCode[1], FuncCode[2], FuncCode[4]);
  and and_42 (and_42_out, FuncCode[3], FuncCode[5]);
  and and_43 (and_43_out, OpCode[1], OpCode[2], OpCode[3]);
  and and_44 (and_44_out, and_43_out, nor_25_out);
  nor nor_25 (nor_25_out, OpCode[0], OpCode[4], OpCode[5]);
  // Priority_Encoder #(.select(4)) priority_encoder_3: pin names not known; wires that end beside it: nop, tunnel_t_t_t_t_t_t, tunnel_t_t_t_t, tunnel_t_t_t_t_t, mult, multu, div, divu, ALU_OP, tunnel_t, tunnel_t_t, \and , \or , \nor , \xor , u, tunnel_t_t_t
  Demultiplexer #(.disabled(0)) demultiplexer_9 (.out0(div), .out1(divu), .in(ds), .sel(FuncCode[0]), .en(and_45_out));
  and and_45 (and_45_out, nor_20_out, and_36_out);
  Demultiplexer #(.tristate("true"), .disabled(0)) demultiplexer_10 (
    .out0(mult), .out1(multu), .in(ms), .sel(FuncCode[0]), .en(and_45_out));
  Demultiplexer #(.enable("false")) demultiplexer_11 (
    .out0(demultiplexer_11_out0), .out1(demultiplexer_11_out1), .in(and_37_out), .sel(FuncCode[0]));
  Demultiplexer #(.enable("false")) demultiplexer_12 (
    .out0(demultiplexer_12_out0), .out1(demultiplexer_12_out1), .in(and_39_out), .sel(OpCode[0]));
  and and_46 (\nor , and_41_out, nor_23_out);
  and and_47 (and_47_out, nor_24_out, and_42_out);
  and and_48 (and_48_out, G_A, demultiplexer_11_out0);
  or or_14 (\and , and_48_out, demultiplexer_12_out0);
  or or_15 (\or , demultiplexer_11_out1, demultiplexer_12_out1);
  and and_49 (and_49_out, G_A, and_47_out);
  or or_16 (\xor , and_49_out, and_44_out);

  assign kbd_rnd = FuncCode[1];

  // Other names for the same wires on the sheet: EI_Selector[1:0] = FuncCode[1:0]; Op[3:0] = ALU_OP;
  //   Selector_Codes[18:0] = SelectorCodes; tty = TTY_Enable

  // Notes on the sheet:
  //   Input_Otput_Region
  //   Decodificacion_por_grupo
  //   Pop_Push
  //   Especial_Ins
  //   Group_A
  //   Group_E
  //   Group_J
  //   Group_C
  //   Group_D
  //   Group_B
  //   Mapeo_Grupo_Selector
  //   Mapeo_Func_ALUCODE
endmodule
