// Logisim project first_alu_implementation.circ as structural Verilog
module ALU_tipo_r (
  input  [31:0] A,
  input  [31:0] B,
  output [31:0] out_3
);

  wire
       Error_de_prestamo_o_desbordamiento_en_resta_sin_signo__a_menor_que_b__se_puede_usar_para_el_comparador_set_less_sin_signo;
  wire [31:0] bits_desbordados_de_la_multiplicacion__si_alguno_es_1_hubo_un_overflow;

  Adder #(.width(32)) adder_1 (.a(A), .b(B), .cin(1'b0));  // open: out, cout
  Subtractor #(.width(32)) subtractor_1 (
    .a(A), .b(B), .bin(1'b0),
    .bout(Error_de_prestamo_o_desbordamiento_en_resta_sin_signo__a_menor_que_b__se_puede_usar_para_el_comparador_set_less_sin_signo));  // open: out
  Multiplier #(.width(32)) multiplier_1 (
    .a(A), .b(B), .cin({32{1'b0}}),
    .cout(bits_desbordados_de_la_multiplicacion__si_alguno_es_1_hubo_un_overflow));  // open: out
  Divider #(.width(32)) divider_1 (.a(A), .b(B), .upper({32{1'b0}}));  // open: out, rem
  Comparator #(.width(32), .mode("unsigned")) comparator_1 (.a(A), .b(B));  // open: gt, eq, lt
  Comparator #(.width(32)) comparator_2 (.a(A), .b(B));  // open: gt, eq, lt
  // AND_Gate and_1 has open pins: in0=A, in1=B, out=open
  Multiplexer #(.width(32)) multiplexer_1 ();  // open: in0, in1, out, sel, en

  // Notes on the sheet:
  //   aqui hay que chequear que B no sea cero
  //   comparador sin signo
  //   comparador con signo
  //   este seria el multiplecer que recibe el func_code y da la salida
endmodule

module restador (
  input  [31:0] in_1,
  input  [31:0] in_2,
  output [31:0] out_3,
  output [31:0] out_4
);

  assign out_4 = ~in_2;  // NOT_Gate not_1, 32 bits wide
  Adder #(.width(32)) adder_1 (.a(in_1), .b(out_4), .out(out_3), .cin(1'b1));  // open: cout
endmodule
